// Logisim project nand2tetris.circ as structural Verilog: 50 circuits, main circuit Computer512x256
module NotGate (
  input  inp,
  output outp
);

  nand nand_1 (outp, inp, inp);
endmodule

module AndGate (
  input  a,
  input  b,
  output outp
);

  wire nand_1_out;

  nand nand_1 (nand_1_out, a, b);
  NotGate notgate_1 (.inp(nand_1_out), .outp(outp));
endmodule

module OrGate (
  input  a,
  input  b,
  output outp
);

  wire notgate_1_outp, notgate_2_outp;

  NotGate notgate_1 (.inp(a), .outp(notgate_1_outp));
  NotGate notgate_2 (.inp(b), .outp(notgate_2_outp));
  nand nand_1 (outp, notgate_1_outp, notgate_2_outp);
endmodule

module XorGate (
  input  in_1,
  input  in_2,
  output out_3
);

  wire nand_1_out, orgate_1_outp;

  nand nand_1 (nand_1_out, in_1, in_2);
  OrGate orgate_1 (.a(in_2), .b(in_1), .outp(orgate_1_outp));
  AndGate andgate_1 (.a(nand_1_out), .b(orgate_1_outp), .outp(out_3));
endmodule

module Mux (
  input  a,
  input  b,
  input  sel,
  output outp
);

  wire andgate_1_outp, andgate_2_outp, notgate_1_outp;

  NotGate notgate_1 (.inp(sel), .outp(notgate_1_outp));
  AndGate andgate_1 (.a(notgate_1_outp), .b(a), .outp(andgate_1_outp));
  AndGate andgate_2 (.a(b), .b(sel), .outp(andgate_2_outp));
  OrGate orgate_1 (.a(andgate_2_outp), .b(andgate_1_outp), .outp(outp));
endmodule

module DMux (
  input  in_1,
  input  in_2,
  output out_3,
  output out_4
);

  wire notgate_1_outp;

  NotGate notgate_1 (.inp(in_2), .outp(notgate_1_outp));
  AndGate andgate_1 (.a(notgate_1_outp), .b(in_1), .outp(out_3));
  AndGate andgate_2 (.a(in_1), .b(in_2), .outp(out_4));
endmodule

module Not16 (
  input  [15:0] in16,
  output [15:0] out16
);

  NotGate notgate_1 (.inp(in16[0]), .outp(out16[0]));
  NotGate notgate_2 (.inp(in16[1]), .outp(out16[1]));
  NotGate notgate_3 (.inp(in16[2]), .outp(out16[2]));
  NotGate notgate_4 (.inp(in16[3]), .outp(out16[3]));
  NotGate notgate_5 (.inp(in16[4]), .outp(out16[4]));
  NotGate notgate_6 (.inp(in16[5]), .outp(out16[5]));
  NotGate notgate_7 (.inp(in16[6]), .outp(out16[6]));
  NotGate notgate_8 (.inp(in16[7]), .outp(out16[7]));
  NotGate notgate_9 (.inp(in16[8]), .outp(out16[8]));
  NotGate notgate_10 (.inp(in16[9]), .outp(out16[9]));
  NotGate notgate_11 (.inp(in16[10]), .outp(out16[10]));
  NotGate notgate_12 (.inp(in16[11]), .outp(out16[11]));
  NotGate notgate_13 (.inp(in16[12]), .outp(out16[12]));
  NotGate notgate_14 (.inp(in16[13]), .outp(out16[13]));
  NotGate notgate_15 (.inp(in16[14]), .outp(out16[14]));
  NotGate notgate_16 (.inp(in16[15]), .outp(out16[15]));
endmodule

module And16 (
  input  [15:0] b16,
  input  [15:0] a16,
  output [15:0] out16
);

  AndGate andgate_1 (.a(a16[0]), .b(b16[0]), .outp(out16[0]));
  AndGate andgate_2 (.a(a16[1]), .b(b16[1]), .outp(out16[1]));
  AndGate andgate_3 (.a(a16[2]), .b(b16[2]), .outp(out16[2]));
  AndGate andgate_4 (.a(a16[3]), .b(b16[3]), .outp(out16[3]));
  AndGate andgate_5 (.a(a16[4]), .b(b16[4]), .outp(out16[4]));
  AndGate andgate_6 (.a(a16[5]), .b(b16[5]), .outp(out16[5]));
  AndGate andgate_7 (.a(a16[6]), .b(b16[6]), .outp(out16[6]));
  AndGate andgate_8 (.a(a16[7]), .b(b16[7]), .outp(out16[7]));
  AndGate andgate_9 (.a(a16[8]), .b(b16[8]), .outp(out16[8]));
  AndGate andgate_10 (.a(a16[9]), .b(b16[9]), .outp(out16[9]));
  AndGate andgate_11 (.a(a16[10]), .b(b16[10]), .outp(out16[10]));
  AndGate andgate_12 (.a(a16[11]), .b(b16[11]), .outp(out16[11]));
  AndGate andgate_13 (.a(a16[12]), .b(b16[12]), .outp(out16[12]));
  AndGate andgate_14 (.a(a16[13]), .b(b16[13]), .outp(out16[13]));
  AndGate andgate_15 (.a(a16[14]), .b(b16[14]), .outp(out16[14]));
  AndGate andgate_16 (.a(a16[15]), .b(b16[15]), .outp(out16[15]));
endmodule

module Or16 (
  input  [15:0] b16,
  input  [15:0] a16,
  output [15:0] out16
);

  OrGate orgate_1 (.a(b16[0]), .b(a16[0]), .outp(out16[0]));
  OrGate orgate_2 (.a(b16[1]), .b(a16[1]), .outp(out16[1]));
  OrGate orgate_3 (.a(b16[2]), .b(a16[2]), .outp(out16[2]));
  OrGate orgate_4 (.a(b16[3]), .b(a16[3]), .outp(out16[3]));
  OrGate orgate_5 (.a(b16[4]), .b(a16[4]), .outp(out16[4]));
  OrGate orgate_6 (.a(b16[5]), .b(a16[5]), .outp(out16[5]));
  OrGate orgate_7 (.a(b16[6]), .b(a16[6]), .outp(out16[6]));
  OrGate orgate_8 (.a(b16[7]), .b(a16[7]), .outp(out16[7]));
  OrGate orgate_9 (.a(b16[8]), .b(a16[8]), .outp(out16[8]));
  OrGate orgate_10 (.a(b16[9]), .b(a16[9]), .outp(out16[9]));
  OrGate orgate_11 (.a(b16[10]), .b(a16[10]), .outp(out16[10]));
  OrGate orgate_12 (.a(b16[11]), .b(a16[11]), .outp(out16[11]));
  OrGate orgate_13 (.a(b16[12]), .b(a16[12]), .outp(out16[12]));
  OrGate orgate_14 (.a(b16[13]), .b(a16[13]), .outp(out16[13]));
  OrGate orgate_15 (.a(b16[14]), .b(a16[14]), .outp(out16[14]));
  OrGate orgate_16 (.a(b16[15]), .b(a16[15]), .outp(out16[15]));
endmodule

module Mux16 (
  input  sel,
  input  [15:0] b16,
  input  [15:0] a16,
  output [15:0] out16
);

  Mux mux_1 (.a(a16[0]), .b(b16[0]), .sel(sel), .outp(out16[0]));
  Mux mux_2 (.a(a16[1]), .b(b16[1]), .sel(sel), .outp(out16[1]));
  Mux mux_3 (.a(a16[2]), .b(b16[2]), .sel(sel), .outp(out16[2]));
  Mux mux_4 (.a(a16[3]), .b(b16[3]), .sel(sel), .outp(out16[3]));
  Mux mux_5 (.a(a16[4]), .b(b16[4]), .sel(sel), .outp(out16[4]));
  Mux mux_6 (.a(a16[5]), .b(b16[5]), .sel(sel), .outp(out16[5]));
  Mux mux_7 (.a(a16[6]), .b(b16[6]), .sel(sel), .outp(out16[6]));
  Mux mux_8 (.a(a16[7]), .b(b16[7]), .sel(sel), .outp(out16[7]));
  Mux mux_9 (.a(a16[8]), .b(b16[8]), .sel(sel), .outp(out16[8]));
  Mux mux_10 (.a(a16[9]), .b(b16[9]), .sel(sel), .outp(out16[9]));
  Mux mux_11 (.a(a16[10]), .b(b16[10]), .sel(sel), .outp(out16[10]));
  Mux mux_12 (.a(a16[11]), .b(b16[11]), .sel(sel), .outp(out16[11]));
  Mux mux_13 (.a(a16[12]), .b(b16[12]), .sel(sel), .outp(out16[12]));
  Mux mux_14 (.a(a16[13]), .b(b16[13]), .sel(sel), .outp(out16[13]));
  Mux mux_15 (.a(a16[14]), .b(b16[14]), .sel(sel), .outp(out16[14]));
  Mux mux_16 (.a(a16[15]), .b(b16[15]), .sel(sel), .outp(out16[15]));
endmodule

module Or8Way (
  input  [7:0] in8,
  output outp
);

  wire orgate_1_outp, orgate_2_outp, orgate_3_outp, orgate_4_outp, orgate_5_outp, orgate_6_outp;

  OrGate orgate_1 (.a(in8[1]), .b(in8[0]), .outp(orgate_1_outp));
  OrGate orgate_2 (.a(in8[2]), .b(orgate_1_outp), .outp(orgate_2_outp));
  OrGate orgate_3 (.a(in8[3]), .b(orgate_2_outp), .outp(orgate_3_outp));
  OrGate orgate_4 (.a(in8[4]), .b(orgate_3_outp), .outp(orgate_4_outp));
  OrGate orgate_5 (.a(in8[5]), .b(orgate_4_outp), .outp(orgate_5_outp));
  OrGate orgate_6 (.a(in8[6]), .b(orgate_5_outp), .outp(orgate_6_outp));
  OrGate orgate_7 (.a(in8[7]), .b(orgate_6_outp), .outp(outp));
endmodule

module Mux4Way16 (
  input  [15:0] a16,
  input  [15:0] b16,
  input  [15:0] c16,
  input  [15:0] d16,
  input  [1:0] sel2,
  output [15:0] out16
);

  wire [15:0] mux16_1_out16, mux16_2_out16;

  Mux16 mux16_1 (.b16(b16), .a16(a16), .sel(sel2[0]), .out16(mux16_1_out16));
  Mux16 mux16_2 (.b16(d16), .a16(c16), .sel(sel2[0]), .out16(mux16_2_out16));
  Mux16 mux16_3 (.b16(mux16_2_out16), .a16(mux16_1_out16), .sel(sel2[1]), .out16(out16));
endmodule

module Mux8Way16 (
  input  [15:0] a16,
  input  [15:0] b16,
  input  [15:0] c16,
  input  [15:0] d16,
  input  [15:0] e16,
  input  [15:0] f16,
  input  [15:0] g16,
  input  [15:0] h16,
  input  [2:0] sel3,
  output [15:0] out16
);

  wire [15:0] mux4way16_1_out16, mux4way16_2_out16;

  Mux4Way16 mux4way16_1 (.a16(a16), .b16(b16), .c16(c16), .d16(d16), .sel2(sel3[1:0]), .out16(mux4way16_1_out16));
  Mux4Way16 mux4way16_2 (.a16(e16), .b16(f16), .c16(g16), .d16(h16), .sel2(sel3[1:0]), .out16(mux4way16_2_out16));
  Mux16 mux16_1 (.b16(mux4way16_2_out16), .a16(mux4way16_1_out16), .sel(sel3[2]), .out16(out16));
endmodule

module DMux4Way (
  input  inp,
  input  [1:0] sel2,
  output a,
  output b,
  output c,
  output d
);

  wire dmux_1_out_3, dmux_1_out_4;

  DMux dmux_1 (.in_1(inp), .in_2(sel2[1]), .out_3(dmux_1_out_3), .out_4(dmux_1_out_4));
  DMux dmux_2 (.in_1(dmux_1_out_3), .in_2(sel2[0]), .out_3(a), .out_4(b));
  DMux dmux_3 (.in_1(dmux_1_out_4), .in_2(sel2[0]), .out_3(c), .out_4(d));
endmodule

module DMux8Way (
  input  inp,
  input  [2:0] sel3,
  output a,
  output b,
  output c,
  output d,
  output e,
  output f,
  output g,
  output h
);

  wire dmux_1_out_3, dmux_1_out_4;

  DMux dmux_1 (.in_1(inp), .in_2(sel3[2]), .out_3(dmux_1_out_3), .out_4(dmux_1_out_4));
  DMux4Way dmux4way_1 (.inp(dmux_1_out_3), .sel2(sel3[1:0]), .a(a), .b(b), .c(c), .d(d));
  DMux4Way dmux4way_2 (.inp(dmux_1_out_4), .sel2(sel3[1:0]), .a(e), .b(f), .c(g), .d(h));
endmodule

module FullAdder (
  input  a,
  input  b,
  input  c,
  output sum,
  output carry
);

  wire halfadder_1_carry, halfadder_1_sum, halfadder_2_carry;

  HalfAdder halfadder_1 (.a(a), .b(b), .sum(halfadder_1_sum), .carry(halfadder_1_carry));
  HalfAdder halfadder_2 (.a(halfadder_1_sum), .b(c), .sum(sum), .carry(halfadder_2_carry));
  OrGate orgate_1 (.a(halfadder_1_carry), .b(halfadder_2_carry), .outp(carry));
endmodule

module HalfAdder (
  input  a,
  input  b,
  output sum,
  output carry
);

  XorGate xorgate_1 (.in_1(b), .in_2(a), .out_3(sum));
  AndGate andgate_1 (.a(a), .b(b), .outp(carry));
endmodule

module Add16 (
  input  [15:0] a16,
  input  [15:0] b16,
  output [15:0] out16
);

  wire fulladder_1_carry, fulladder_2_carry, fulladder_3_carry, fulladder_4_carry, fulladder_5_carry,
       fulladder_6_carry, fulladder_7_carry, fulladder_8_carry, fulladder_9_carry, fulladder_10_carry,
       fulladder_11_carry, fulladder_12_carry, fulladder_13_carry, fulladder_14_carry, halfadder_1_carry;

  HalfAdder halfadder_1 (.a(a16[0]), .b(b16[0]), .sum(out16[0]), .carry(halfadder_1_carry));
  FullAdder fulladder_1 (.a(a16[1]), .b(halfadder_1_carry), .c(b16[1]), .sum(out16[1]), .carry(fulladder_1_carry));
  FullAdder fulladder_2 (.a(a16[2]), .b(fulladder_1_carry), .c(b16[2]), .sum(out16[2]), .carry(fulladder_2_carry));
  FullAdder fulladder_3 (.a(a16[3]), .b(fulladder_2_carry), .c(b16[3]), .sum(out16[3]), .carry(fulladder_3_carry));
  FullAdder fulladder_4 (.a(a16[4]), .b(fulladder_3_carry), .c(b16[4]), .sum(out16[4]), .carry(fulladder_4_carry));
  FullAdder fulladder_5 (.a(a16[5]), .b(fulladder_4_carry), .c(b16[5]), .sum(out16[5]), .carry(fulladder_5_carry));
  FullAdder fulladder_6 (.a(a16[6]), .b(fulladder_5_carry), .c(b16[6]), .sum(out16[6]), .carry(fulladder_6_carry));
  FullAdder fulladder_7 (.a(a16[7]), .b(fulladder_6_carry), .c(b16[7]), .sum(out16[7]), .carry(fulladder_7_carry));
  FullAdder fulladder_8 (.a(a16[8]), .b(fulladder_7_carry), .c(b16[8]), .sum(out16[8]), .carry(fulladder_8_carry));
  FullAdder fulladder_9 (.a(a16[9]), .b(fulladder_8_carry), .c(b16[9]), .sum(out16[9]), .carry(fulladder_9_carry));
  FullAdder fulladder_10 (.a(a16[10]), .b(fulladder_9_carry), .c(b16[10]), .sum(out16[10]), .carry(fulladder_10_carry));
  FullAdder fulladder_11 (
    .a(a16[11]), .b(fulladder_10_carry), .c(b16[11]), .sum(out16[11]), .carry(fulladder_11_carry));
  FullAdder fulladder_12 (
    .a(a16[12]), .b(fulladder_11_carry), .c(b16[12]), .sum(out16[12]), .carry(fulladder_12_carry));
  FullAdder fulladder_13 (
    .a(a16[13]), .b(fulladder_12_carry), .c(b16[13]), .sum(out16[13]), .carry(fulladder_13_carry));
  FullAdder fulladder_14 (
    .a(a16[14]), .b(fulladder_13_carry), .c(b16[14]), .sum(out16[14]), .carry(fulladder_14_carry));
  FullAdder fulladder_15 (.a(a16[15]), .b(fulladder_14_carry), .c(b16[15]), .sum(out16[15]));  // open: carry
endmodule

module Inc16 (
  input  [15:0] in16,
  output [15:0] out16
);

  wire halfadder_1_carry, halfadder_2_carry, halfadder_3_carry, halfadder_4_carry, halfadder_5_carry,
       halfadder_6_carry, halfadder_7_carry, halfadder_8_carry, halfadder_9_carry, halfadder_10_carry,
       halfadder_11_carry, halfadder_12_carry, halfadder_13_carry, halfadder_14_carry, halfadder_15_carry;

  HalfAdder halfadder_1 (.a(1'b1), .b(in16[0]), .sum(out16[0]), .carry(halfadder_1_carry));
  HalfAdder halfadder_2 (.a(halfadder_1_carry), .b(in16[1]), .sum(out16[1]), .carry(halfadder_2_carry));
  HalfAdder halfadder_3 (.a(halfadder_2_carry), .b(in16[2]), .sum(out16[2]), .carry(halfadder_3_carry));
  HalfAdder halfadder_4 (.a(halfadder_3_carry), .b(in16[3]), .sum(out16[3]), .carry(halfadder_4_carry));
  HalfAdder halfadder_5 (.a(halfadder_4_carry), .b(in16[4]), .sum(out16[4]), .carry(halfadder_5_carry));
  HalfAdder halfadder_6 (.a(halfadder_5_carry), .b(in16[5]), .sum(out16[5]), .carry(halfadder_6_carry));
  HalfAdder halfadder_7 (.a(halfadder_6_carry), .b(in16[6]), .sum(out16[6]), .carry(halfadder_7_carry));
  HalfAdder halfadder_8 (.a(halfadder_7_carry), .b(in16[7]), .sum(out16[7]), .carry(halfadder_8_carry));
  HalfAdder halfadder_9 (.a(halfadder_8_carry), .b(in16[8]), .sum(out16[8]), .carry(halfadder_9_carry));
  HalfAdder halfadder_10 (.a(halfadder_9_carry), .b(in16[9]), .sum(out16[9]), .carry(halfadder_10_carry));
  HalfAdder halfadder_11 (.a(halfadder_10_carry), .b(in16[10]), .sum(out16[10]), .carry(halfadder_11_carry));
  HalfAdder halfadder_12 (.a(halfadder_11_carry), .b(in16[11]), .sum(out16[11]), .carry(halfadder_12_carry));
  HalfAdder halfadder_13 (.a(halfadder_12_carry), .b(in16[12]), .sum(out16[12]), .carry(halfadder_13_carry));
  HalfAdder halfadder_14 (.a(halfadder_13_carry), .b(in16[13]), .sum(out16[13]), .carry(halfadder_14_carry));
  HalfAdder halfadder_15 (.a(halfadder_14_carry), .b(in16[14]), .sum(out16[14]), .carry(halfadder_15_carry));
  HalfAdder halfadder_16 (.a(halfadder_15_carry), .b(in16[15]), .sum(out16[15]));  // open: carry
endmodule

module ALU (
  input  zx,
  input  nx,
  input  zy,
  input  ny,
  input  f,
  input  no,
  input  [15:0] x16,
  input  [15:0] y16,
  output [15:0] out16,
  output zr,
  output ng
);

  wire or8way_1_outp, or8way_2_outp, orgate_1_outp;
  wire [15:0] add16_1_out16, and16_1_out16, mux16_1_out16, mux16_2_out16, mux16_3_out16, mux16_4_out16,
       mux16_5_out16, not16_1_out16, not16_2_out16, not16_3_out16;

  Mux16 mux16_1 (.b16({16{1'b0}}), .a16(x16), .sel(zx), .out16(mux16_1_out16));
  Mux16 mux16_2 (.b16({16{1'b0}}), .a16(y16), .sel(zy), .out16(mux16_2_out16));
  Not16 not16_1 (.in16(mux16_1_out16), .out16(not16_1_out16));
  Not16 not16_2 (.in16(mux16_2_out16), .out16(not16_2_out16));
  Mux16 mux16_3 (.b16(not16_1_out16), .a16(mux16_1_out16), .sel(nx), .out16(mux16_3_out16));
  Mux16 mux16_4 (.b16(not16_2_out16), .a16(mux16_2_out16), .sel(ny), .out16(mux16_4_out16));
  And16 and16_1 (.b16(mux16_4_out16), .a16(mux16_3_out16), .out16(and16_1_out16));
  Add16 add16_1 (.a16(mux16_3_out16), .b16(mux16_4_out16), .out16(add16_1_out16));
  Mux16 mux16_5 (.b16(add16_1_out16), .a16(and16_1_out16), .sel(f), .out16(mux16_5_out16));
  Not16 not16_3 (.in16(mux16_5_out16), .out16(not16_3_out16));
  Mux16 mux16_6 (.b16(not16_3_out16), .a16(mux16_5_out16), .sel(no), .out16({ng, out16[14:0]}));
  Or8Way or8way_1 (.in8(out16[7:0]), .outp(or8way_1_outp));
  Or8Way or8way_2 (.in8({ng, out16[14:8]}), .outp(or8way_2_outp));
  OrGate orgate_1 (.a(or8way_2_outp), .b(or8way_1_outp), .outp(orgate_1_outp));
  NotGate notgate_1 (.inp(orgate_1_outp), .outp(zr));

  assign out16[15] = ng;
endmodule

module Bit (
  input  load,
  input  inp,
  input  clk,
  output outp
);

  wire mux_1_outp;

  Mux mux_1 (.a(outp), .b(inp), .sel(load), .outp(mux_1_outp));
  D_Flip_Flop d_ff_1 (.D(mux_1_outp), .clk(clk), .Q(outp));  // open: Qn, preset, reset
endmodule

module Register16 (
  input  clk,
  input  load,
  input  [15:0] in16,
  output [15:0] out16
);

  Bit bit_1 (.inp(in16[0]), .load(load), .clk(clk), .outp(out16[0]));
  Bit bit_2 (.inp(in16[1]), .load(load), .clk(clk), .outp(out16[1]));
  Bit bit_3 (.inp(in16[2]), .load(load), .clk(clk), .outp(out16[2]));
  Bit bit_4 (.inp(in16[3]), .load(load), .clk(clk), .outp(out16[3]));
  Bit bit_5 (.inp(in16[4]), .load(load), .clk(clk), .outp(out16[4]));
  Bit bit_6 (.inp(in16[5]), .load(load), .clk(clk), .outp(out16[5]));
  Bit bit_7 (.inp(in16[6]), .load(load), .clk(clk), .outp(out16[6]));
  Bit bit_8 (.inp(in16[7]), .load(load), .clk(clk), .outp(out16[7]));
  Bit bit_9 (.inp(in16[8]), .load(load), .clk(clk), .outp(out16[8]));
  Bit bit_10 (.inp(in16[9]), .load(load), .clk(clk), .outp(out16[9]));
  Bit bit_11 (.inp(in16[10]), .load(load), .clk(clk), .outp(out16[10]));
  Bit bit_12 (.inp(in16[11]), .load(load), .clk(clk), .outp(out16[11]));
  Bit bit_13 (.inp(in16[12]), .load(load), .clk(clk), .outp(out16[12]));
  Bit bit_14 (.inp(in16[13]), .load(load), .clk(clk), .outp(out16[13]));
  Bit bit_15 (.inp(in16[14]), .load(load), .clk(clk), .outp(out16[14]));
  Bit bit_16 (.inp(in16[15]), .load(load), .clk(clk), .outp(out16[15]));
endmodule

module RAM8 (
  input  load,
  input  clk,
  input  [15:0] in16,
  input  [2:0] address,
  output [15:0] out16
);

  wire dmux8way_1_a, dmux8way_1_b, dmux8way_1_c, dmux8way_1_d, dmux8way_1_e, dmux8way_1_f, dmux8way_1_g,
       dmux8way_1_h;
  wire [15:0] register16_1_out16, register16_2_out16, register16_3_out16, register16_4_out16,
       register16_5_out16, register16_6_out16, register16_7_out16, register16_8_out16;

  DMux8Way dmux8way_1 (
    .inp(load), .sel3(address), .a(dmux8way_1_a), .b(dmux8way_1_b), .c(dmux8way_1_c), .d(dmux8way_1_d),
    .e(dmux8way_1_e), .f(dmux8way_1_f), .g(dmux8way_1_g), .h(dmux8way_1_h));
  Register16 register16_1 (.in16(in16), .clk(clk), .load(dmux8way_1_a), .out16(register16_1_out16));
  Register16 register16_2 (.in16(in16), .clk(clk), .load(dmux8way_1_b), .out16(register16_2_out16));
  Register16 register16_3 (.in16(in16), .clk(clk), .load(dmux8way_1_c), .out16(register16_3_out16));
  Register16 register16_4 (.in16(in16), .clk(clk), .load(dmux8way_1_d), .out16(register16_4_out16));
  Register16 register16_5 (.in16(in16), .clk(clk), .load(dmux8way_1_e), .out16(register16_5_out16));
  Register16 register16_6 (.in16(in16), .clk(clk), .load(dmux8way_1_f), .out16(register16_6_out16));
  Register16 register16_7 (.in16(in16), .clk(clk), .load(dmux8way_1_g), .out16(register16_7_out16));
  Register16 register16_8 (.in16(in16), .clk(clk), .load(dmux8way_1_h), .out16(register16_8_out16));
  Mux8Way16 mux8way16_1 (
    .sel3(address), .a16(register16_1_out16), .b16(register16_2_out16), .c16(register16_3_out16),
    .d16(register16_4_out16), .e16(register16_5_out16), .f16(register16_6_out16), .g16(register16_7_out16),
    .h16(register16_8_out16), .out16(out16));
endmodule

module RAM8BuiltIn (
  input  [2:0] address,
  input  load,
  input  clk,
  input  [15:0] in16,
  output [15:0] out16
);

  RAM #(.addrWidth(3), .dataWidth(16), .enables("line")) ram_1 (
    .addr(address), .we(load), .clk(clk), .din(in16), .dout(out16));
endmodule

module RAM64 (
  input  load,
  input  clk,
  input  [15:0] in16,
  input  [5:0] address,
  output [15:0] out16
);

  wire dmux8way_1_a, dmux8way_1_b, dmux8way_1_c, dmux8way_1_d, dmux8way_1_e, dmux8way_1_f, dmux8way_1_g,
       dmux8way_1_h;
  wire [15:0] ram8builtin_1_out16, ram8builtin_2_out16, ram8builtin_3_out16, ram8builtin_4_out16,
       ram8builtin_5_out16, ram8builtin_6_out16, ram8builtin_7_out16, ram8builtin_8_out16;

  DMux8Way dmux8way_1 (
    .inp(load), .sel3(address[2:0]), .a(dmux8way_1_a), .b(dmux8way_1_b), .c(dmux8way_1_c), .d(dmux8way_1_d),
    .e(dmux8way_1_e), .f(dmux8way_1_f), .g(dmux8way_1_g), .h(dmux8way_1_h));
  RAM8BuiltIn ram8builtin_1 (
    .load(dmux8way_1_a), .address(address[5:3]), .in16(in16), .clk(clk), .out16(ram8builtin_1_out16));
  RAM8BuiltIn ram8builtin_2 (
    .load(dmux8way_1_b), .address(address[5:3]), .in16(in16), .clk(clk), .out16(ram8builtin_2_out16));
  RAM8BuiltIn ram8builtin_3 (
    .load(dmux8way_1_c), .address(address[5:3]), .in16(in16), .clk(clk), .out16(ram8builtin_3_out16));
  RAM8BuiltIn ram8builtin_4 (
    .load(dmux8way_1_d), .address(address[5:3]), .in16(in16), .clk(clk), .out16(ram8builtin_4_out16));
  RAM8BuiltIn ram8builtin_5 (
    .load(dmux8way_1_e), .address(address[5:3]), .in16(in16), .clk(clk), .out16(ram8builtin_5_out16));
  RAM8BuiltIn ram8builtin_6 (
    .load(dmux8way_1_f), .address(address[5:3]), .in16(in16), .clk(clk), .out16(ram8builtin_6_out16));
  RAM8BuiltIn ram8builtin_7 (
    .load(dmux8way_1_g), .address(address[5:3]), .in16(in16), .clk(clk), .out16(ram8builtin_7_out16));
  RAM8BuiltIn ram8builtin_8 (
    .load(dmux8way_1_h), .address(address[5:3]), .in16(in16), .clk(clk), .out16(ram8builtin_8_out16));
  Mux8Way16 mux8way16_1 (
    .sel3(address[2:0]), .a16(ram8builtin_1_out16), .b16(ram8builtin_2_out16), .c16(ram8builtin_3_out16),
    .d16(ram8builtin_4_out16), .e16(ram8builtin_5_out16), .f16(ram8builtin_6_out16),
    .g16(ram8builtin_7_out16), .h16(ram8builtin_8_out16), .out16(out16));
endmodule

module RAM64BuiltIn (
  input  [5:0] address,
  input  load,
  input  clk,
  input  [15:0] in16,
  output [15:0] out16
);

  RAM #(.addrWidth(6), .dataWidth(16), .enables("line")) ram_1 (
    .addr(address), .we(load), .clk(clk), .din(in16), .dout(out16));
endmodule

module RAM512 (
  input  load,
  input  clk,
  input  [15:0] in16,
  input  [8:0] address,
  output [15:0] out16
);

  wire dmux8way_1_a, dmux8way_1_b, dmux8way_1_c, dmux8way_1_d, dmux8way_1_e, dmux8way_1_f, dmux8way_1_g,
       dmux8way_1_h;
  wire [15:0] ram64builtin_1_out16, ram64builtin_2_out16, ram64builtin_3_out16, ram64builtin_4_out16,
       ram64builtin_5_out16, ram64builtin_6_out16, ram64builtin_7_out16, ram64builtin_8_out16;

  DMux8Way dmux8way_1 (
    .inp(load), .sel3(address[2:0]), .a(dmux8way_1_a), .b(dmux8way_1_b), .c(dmux8way_1_c), .d(dmux8way_1_d),
    .e(dmux8way_1_e), .f(dmux8way_1_f), .g(dmux8way_1_g), .h(dmux8way_1_h));
  RAM64BuiltIn ram64builtin_1 (
    .load(dmux8way_1_a), .address(address[8:3]), .in16(in16), .clk(clk), .out16(ram64builtin_1_out16));
  RAM64BuiltIn ram64builtin_2 (
    .load(dmux8way_1_b), .address(address[8:3]), .in16(in16), .clk(clk), .out16(ram64builtin_2_out16));
  RAM64BuiltIn ram64builtin_3 (
    .load(dmux8way_1_c), .address(address[8:3]), .in16(in16), .clk(clk), .out16(ram64builtin_3_out16));
  RAM64BuiltIn ram64builtin_4 (
    .load(dmux8way_1_d), .address(address[8:3]), .in16(in16), .clk(clk), .out16(ram64builtin_4_out16));
  RAM64BuiltIn ram64builtin_5 (
    .load(dmux8way_1_e), .address(address[8:3]), .in16(in16), .clk(clk), .out16(ram64builtin_5_out16));
  RAM64BuiltIn ram64builtin_6 (
    .load(dmux8way_1_f), .address(address[8:3]), .in16(in16), .clk(clk), .out16(ram64builtin_6_out16));
  RAM64BuiltIn ram64builtin_7 (
    .load(dmux8way_1_g), .address(address[8:3]), .in16(in16), .clk(clk), .out16(ram64builtin_7_out16));
  RAM64BuiltIn ram64builtin_8 (
    .load(dmux8way_1_h), .address(address[8:3]), .in16(in16), .clk(clk), .out16(ram64builtin_8_out16));
  Mux8Way16 mux8way16_1 (
    .sel3(address[2:0]), .a16(ram64builtin_1_out16), .b16(ram64builtin_2_out16), .c16(ram64builtin_3_out16),
    .d16(ram64builtin_4_out16), .e16(ram64builtin_5_out16), .f16(ram64builtin_6_out16),
    .g16(ram64builtin_7_out16), .h16(ram64builtin_8_out16), .out16(out16));
endmodule

module RAM512BuiltIn (
  input  [8:0] address,
  input  load,
  input  clk,
  input  [15:0] in16,
  output [15:0] out16
);

  RAM #(.addrWidth(9), .dataWidth(16), .enables("line")) ram_1 (
    .addr(address), .we(load), .clk(clk), .din(in16), .dout(out16));
endmodule

module RAM4K (
  input  load,
  input  clk,
  input  [15:0] in16,
  input  [11:0] address,
  output [15:0] out16
);

  wire dmux8way_1_a, dmux8way_1_b, dmux8way_1_c, dmux8way_1_d, dmux8way_1_e, dmux8way_1_f, dmux8way_1_g,
       dmux8way_1_h;
  wire [15:0] ram512builtin_1_out16, ram512builtin_2_out16, ram512builtin_3_out16, ram512builtin_4_out16,
       ram512builtin_5_out16, ram512builtin_6_out16, ram512builtin_7_out16, ram512builtin_8_out16;

  DMux8Way dmux8way_1 (
    .inp(load), .sel3(address[2:0]), .a(dmux8way_1_a), .b(dmux8way_1_b), .c(dmux8way_1_c), .d(dmux8way_1_d),
    .e(dmux8way_1_e), .f(dmux8way_1_f), .g(dmux8way_1_g), .h(dmux8way_1_h));
  RAM512BuiltIn ram512builtin_1 (
    .load(dmux8way_1_a), .address(address[11:3]), .in16(in16), .clk(clk), .out16(ram512builtin_1_out16));
  RAM512BuiltIn ram512builtin_2 (
    .load(dmux8way_1_b), .address(address[11:3]), .in16(in16), .clk(clk), .out16(ram512builtin_2_out16));
  RAM512BuiltIn ram512builtin_3 (
    .load(dmux8way_1_c), .address(address[11:3]), .in16(in16), .clk(clk), .out16(ram512builtin_3_out16));
  RAM512BuiltIn ram512builtin_4 (
    .load(dmux8way_1_d), .address(address[11:3]), .in16(in16), .clk(clk), .out16(ram512builtin_4_out16));
  RAM512BuiltIn ram512builtin_5 (
    .load(dmux8way_1_e), .address(address[11:3]), .in16(in16), .clk(clk), .out16(ram512builtin_5_out16));
  RAM512BuiltIn ram512builtin_6 (
    .load(dmux8way_1_f), .address(address[11:3]), .in16(in16), .clk(clk), .out16(ram512builtin_6_out16));
  RAM512BuiltIn ram512builtin_7 (
    .load(dmux8way_1_g), .address(address[11:3]), .in16(in16), .clk(clk), .out16(ram512builtin_7_out16));
  RAM512BuiltIn ram512builtin_8 (
    .load(dmux8way_1_h), .address(address[11:3]), .in16(in16), .clk(clk), .out16(ram512builtin_8_out16));
  Mux8Way16 mux8way16_1 (
    .sel3(address[2:0]), .a16(ram512builtin_1_out16), .b16(ram512builtin_2_out16),
    .c16(ram512builtin_3_out16), .d16(ram512builtin_4_out16), .e16(ram512builtin_5_out16),
    .f16(ram512builtin_6_out16), .g16(ram512builtin_7_out16), .h16(ram512builtin_8_out16), .out16(out16));
endmodule

module RAM4KBuiltIn (
  input  [11:0] address,
  input  load,
  input  clk,
  input  [15:0] in16,
  output [15:0] out16
);

  RAM #(.addrWidth(12), .dataWidth(16), .enables("line")) ram_1 (
    .addr(address), .we(load), .clk(clk), .din(in16), .dout(out16));
endmodule

module RAM16K (
  input  load,
  input  clk,
  input  [15:0] in16,
  input  [13:0] address,
  output [15:0] out16
);

  wire dmux4way_1_a, dmux4way_1_b, dmux4way_1_c, dmux4way_1_d;
  wire [15:0] ram4kbuiltin_1_out16, ram4kbuiltin_2_out16, ram4kbuiltin_3_out16, ram4kbuiltin_4_out16;

  DMux4Way dmux4way_1 (
    .inp(load), .sel2(address[1:0]), .a(dmux4way_1_a), .b(dmux4way_1_b), .c(dmux4way_1_c), .d(dmux4way_1_d));
  RAM4KBuiltIn ram4kbuiltin_1 (
    .load(dmux4way_1_a), .address(address[13:2]), .in16(in16), .clk(clk), .out16(ram4kbuiltin_1_out16));
  RAM4KBuiltIn ram4kbuiltin_2 (
    .load(dmux4way_1_b), .address(address[13:2]), .in16(in16), .clk(clk), .out16(ram4kbuiltin_2_out16));
  RAM4KBuiltIn ram4kbuiltin_3 (
    .load(dmux4way_1_c), .address(address[13:2]), .in16(in16), .clk(clk), .out16(ram4kbuiltin_3_out16));
  RAM4KBuiltIn ram4kbuiltin_4 (
    .load(dmux4way_1_d), .address(address[13:2]), .in16(in16), .clk(clk), .out16(ram4kbuiltin_4_out16));
  Mux4Way16 mux4way16_1 (
    .a16(ram4kbuiltin_1_out16), .b16(ram4kbuiltin_2_out16), .c16(ram4kbuiltin_3_out16),
    .d16(ram4kbuiltin_4_out16), .sel2(address[1:0]), .out16(out16));
endmodule

module PC (
  input  inc,
  input  load,
  input  reset,
  input  clk,
  input  [15:0] in16,
  output [15:0] out16
);

  wire [15:0] inc16_1_out16, mux16_1_out16, mux16_2_out16, mux16_3_out16;

  Mux16 mux16_1 (.b16(inc16_1_out16), .a16(out16), .sel(inc), .out16(mux16_1_out16));
  Mux16 mux16_2 (.b16(in16), .a16(mux16_1_out16), .sel(load), .out16(mux16_2_out16));
  Mux16 mux16_3 (.b16({16{1'b0}}), .a16(mux16_2_out16), .sel(reset), .out16(mux16_3_out16));
  Register16 register16_1 (.in16(mux16_3_out16), .clk(clk), .load(1'b1), .out16(out16));
  Inc16 inc16_1 (.in16(out16), .out16(inc16_1_out16));
endmodule

module RAM16KBuiltIn (
  input  [13:0] address,
  input  load,
  input  clk,
  input  [15:0] in16,
  output [15:0] out16
);

  RAM #(.addrWidth(14), .dataWidth(16), .enables("line")) ram_1 (
    .addr(address), .we(load), .clk(clk), .din(in16), .dout(out16));
endmodule

module Memory (
  input  load,
  input  clk,
  input  [15:0] in16,
  input  [14:0] address15,
  output [15:0] out16
);

  wire dmux_1_out_3, dmux_1_out_4, dmux_2_out_3, dmux_2_out_4, dmux_3_out_3, dmux_3_out_4;
  wire [15:0] mux16_1_out16, mux16_2_out16, ram4kbuiltin_1_out16, ram4kbuiltin_2_out16,
       ram16kbuiltin_1_out16, register16_1_out16;

  DMux dmux_1 (.in_1(load), .in_2(address15[14]), .out_3(dmux_1_out_3), .out_4(dmux_1_out_4));
  DMux dmux_2 (.in_1(dmux_1_out_4), .in_2(address15[12]), .out_3(dmux_2_out_3), .out_4(dmux_2_out_4));
  DMux dmux_3 (.in_1(dmux_2_out_3), .in_2(address15[13]), .out_3(dmux_3_out_3), .out_4(dmux_3_out_4));
  RAM16KBuiltIn ram16kbuiltin_1 (
    .load(dmux_1_out_3), .address(address15[13:0]), .in16(in16), .clk(clk), .out16(ram16kbuiltin_1_out16));
  RAM4KBuiltIn ram4kbuiltin_1 (
    .load(dmux_3_out_3), .address(address15[11:0]), .in16(in16), .clk(clk), .out16(ram4kbuiltin_1_out16));
  RAM4KBuiltIn ram4kbuiltin_2 (
    .load(dmux_2_out_4), .address(address15[11:0]), .in16(in16), .clk(clk), .out16(ram4kbuiltin_2_out16));
  Register16 register16_1 (.in16(in16), .clk(clk), .load(dmux_3_out_4), .out16(register16_1_out16));
  Mux16 mux16_1 (.b16(ram4kbuiltin_2_out16), .a16(ram4kbuiltin_1_out16), .sel(address15[12]), .out16(mux16_1_out16));
  Mux16 mux16_2 (.b16(register16_1_out16), .a16(mux16_1_out16), .sel(address15[13]), .out16(mux16_2_out16));
  Mux16 mux16_3 (.b16(mux16_2_out16), .a16(ram16kbuiltin_1_out16), .sel(address15[14]), .out16(out16));

  // Notes on the sheet:
  //   RAM
  //   Screen1
  //   Screen2
  //   Keyboard
endmodule

module DualPortRAM8K (
  input  clk,
  input  [15:0] in16,
  input  load,
  input  [12:0] a_address,
  input  [12:0] b_address,
  output [15:0] a_out,
  output [15:0] b_out
);

  wire and_1_out, clk_read, clk_write;
  wire [12:0] multiplexer_1_out;

  and and_1 (and_1_out, load, clk_write);
  Multiplexer #(.width(13)) multiplexer_1 (.in0(a_address), .in1(b_address), .out(multiplexer_1_out), .sel(clk_read));
  Counter #(.max('h1), .width(1)) counter_1 (.Q(clk_read), .clk(clk));  // open: load, D, count, carry, up, clr
  not not_1 (clk_write, clk_read);
  RAM #(.addrWidth(13), .asyncread("true"), .dataWidth(16)) ram_1 (
    .addr(a_address), .we(and_1_out), .clk(clk), .din(in16), .dout(a_out));  // open: oe
  RAM #(.addrWidth(13), .asyncread("true"), .dataWidth(16)) ram_2 (
    .addr(multiplexer_1_out), .we(and_1_out), .clk(clk), .din(in16), .dout(b_out));  // open: oe

  // Notes on the sheet:
  //   out values will be valid at the system clk frequency
  //   has to be 2x the system clk
endmodule

module VideoCard512x256 (
  input  reset,
  input  clk,
  input  [15:0] inM,
  output outValue,
  output [12:0] addressM,
  output [8:0] x,
  output [7:0] y
);

  wire and_1_out, and_2_out, and_3_out, and_4_out, register_1_q, register_2_q;
  wire [3:0] \bit ;

  Register #(.width(1)) register_1 (.D(and_4_out), .en(clk), .clk(clk), .Q(register_1_q));  // open: clr
  Register #(.width(1)) register_2 (.D(and_1_out), .en(clk), .clk(clk), .Q(register_2_q));  // open: clr
  Counter #(.max('h1fff), .width(13)) counter_1 (
    .load(and_3_out), .D({13{1'b0}}), .count(register_1_q), .Q(addressM), .clk(register_1_q), .clr(reset));  // open: carry, up
  Counter #(.max('h1ff), .width(9)) counter_2 (
    .load(and_1_out), .D({9{1'b0}}), .count(clk), .Q(x), .clk(clk), .clr(reset));  // open: carry, up
  Counter counter_3 (
    .load(and_2_out), .D({8{1'b0}}), .count(register_2_q), .Q(y), .clk(register_2_q), .clr(reset));  // open: carry, up
  and and_1 (and_1_out, x[0], x[1], x[2], x[3], x[4], x[5], x[6], x[7], x[8]);
  and and_2 (and_2_out, y[0], y[1], y[2], y[3], y[4], y[5], y[6], y[7]);
  and and_3 (and_3_out, addressM[0], addressM[1], addressM[2], addressM[3], addressM[4], addressM[5], addressM[6], addressM[7], addressM[8], addressM[9], addressM[10], addressM[11], addressM[12]);
  Multiplexer #(.select(4)) multiplexer_1 (
    .in0(inM[0]), .in1(inM[1]), .in2(inM[2]), .in3(inM[3]), .in4(inM[4]), .in5(inM[5]), .in6(inM[6]),
    .in7(inM[7]), .in8(inM[8]), .in9(inM[9]), .in10(inM[10]), .in11(inM[11]), .in12(inM[12]), .in13(inM[13]),
    .in14(inM[14]), .in15(inM[15]), .out(outValue), .sel(\bit ));
  Counter #(.max('hf), .width(4)) counter_4 (
    .load(and_4_out), .D(4'b0000), .Q(\bit ), .clk(clk), .clr(reset));  // open: count, carry, up
  and and_4 (and_4_out, \bit [0], \bit [1], \bit [2], \bit [3]);

  // Notes on the sheet:
  //   Counting X
  //   Counting Y
  //   Counting the RAM address
  //   addr++ after bit passes 15
  //   y++ after x passes 255
  //   == 8191
  //   Counting the bits in the 16-bit registers
  //   == 15
endmodule

module VideoCard128x128 (
  input  reset,
  input  clk,
  input  [15:0] inM,
  output outValue,
  output [12:0] addressM,
  output [6:0] x,
  output [6:0] y
);

  wire and_1_out, and_2_out, and_3_out, and_4_out, register_1_q, register_2_q;
  wire [3:0] \bit ;

  Register #(.width(1)) register_1 (.D(and_4_out), .en(clk), .clk(clk), .Q(register_1_q));  // open: clr
  Register #(.width(1)) register_2 (.D(and_1_out), .en(clk), .clk(clk), .Q(register_2_q));  // open: clr
  Counter #(.max('h1fff), .width(13)) counter_1 (
    .load(and_3_out), .D({13{1'b0}}), .count(register_1_q), .Q(addressM), .clk(register_1_q), .clr(reset));  // open: carry, up
  Counter #(.max('h7f), .width(7)) counter_2 (
    .load(and_1_out), .D({7{1'b0}}), .count(clk), .Q(x), .clk(clk), .clr(reset));  // open: carry, up
  Counter #(.max('h7f), .width(7)) counter_3 (
    .load(and_2_out), .D({7{1'b0}}), .count(register_2_q), .Q(y), .clk(register_2_q), .clr(reset));  // open: carry, up
  and and_1 (and_1_out, x[0], x[1], x[2], x[3], x[4], x[5], x[6]);
  and and_2 (and_2_out, y[0], y[1], y[2], y[3], y[4], y[5], y[6]);
  Multiplexer #(.select(4)) multiplexer_1 (
    .in0(inM[0]), .in1(inM[1]), .in2(inM[2]), .in3(inM[3]), .in4(inM[4]), .in5(inM[5]), .in6(inM[6]),
    .in7(inM[7]), .in8(inM[8]), .in9(inM[9]), .in10(inM[10]), .in11(inM[11]), .in12(inM[12]), .in13(inM[13]),
    .in14(inM[14]), .in15(inM[15]), .out(outValue), .sel(\bit ));
  and and_3 (and_3_out, addressM[0], addressM[1], addressM[2], addressM[3], addressM[4], addressM[5], addressM[6], addressM[7], addressM[8], addressM[9]);
  Counter #(.max('hf), .width(4)) counter_4 (
    .load(and_4_out), .D(4'b0000), .Q(\bit ), .clk(clk), .clr(reset));  // open: count, carry, up
  and and_4 (and_4_out, \bit [0], \bit [1], \bit [2], \bit [3]);

  // Notes on the sheet:
  //   Counting X
  //   Counting Y
  //   Counting the RAM address
  //   y++ after x passes 127
  //   == 1023
  //   Counting the bits in the 16-bit registers
  //   == 15
endmodule

module VideoCard512x256Test (
  input  in_1,
  input  [15:0] in_2
);

  wire clk, rgb_video_1_p3;
  wire [2:2] rgb_video_1_p6;
  wire [7:0] rgb_video_1_p5;
  wire [8:0] rgb_video_1_p4;
  wire [12:0] videocard512x256_1_addressm;
  wire [15:0] ram_1_dout;

  Clock clock_1 (.out(clk));
  RAM #(.addrWidth(13), .dataWidth(16)) ram_1 (
    .addr(videocard512x256_1_addressm), .clk(clk), .dout(ram_1_dout));  // open: we, oe, din
  // RGB_Video #(.cursor("No Cursor"), .height(256), .width(256)) rgb_video_1: pin names not known; wires that end beside it: in_1, clk, rgb_video_1_p3, rgb_video_1_p4[7:0], rgb_video_1_p5, {3{rgb_video_1_p6[2]}}, ram_1_dout
  not not_1 (rgb_video_1_p3, rgb_video_1_p4[8]);
  VideoCard512x256 videocard512x256_1 (
    .clk(clk), .inM(in_2), .y(rgb_video_1_p5), .x(rgb_video_1_p4), .addressM(videocard512x256_1_addressm),
    .outValue(rgb_video_1_p6[2]));  // open: reset
  // RGB_Video #(.cursor("No Cursor"), .height(256), .width(256)) rgb_video_2: pin names not known; wires that end beside it: in_1, clk, rgb_video_1_p4[8], rgb_video_1_p4[7:0], rgb_video_1_p5, {3{rgb_video_1_p6[2]}}
endmodule

module VideoCard128x128Test (
  input  in_1,
  input  [15:0] in_2
);

  wire clk;
  wire [2:2] videocard128x128_1_outvalue;
  wire [6:0] videocard128x128_1_x, videocard128x128_1_y;
  wire [12:0] videocard128x128_1_addressm;
  wire [15:0] ram_1_dout;

  Clock clock_1 (.out(clk));
  RAM #(.addrWidth(13), .dataWidth(16)) ram_1 (
    .addr(videocard128x128_1_addressm), .clk(clk), .dout(ram_1_dout));  // open: we, oe, din
  VideoCard128x128 videocard128x128_1 (
    .clk(clk), .inM(in_2), .y(videocard128x128_1_y), .x(videocard128x128_1_x),
    .addressM(videocard128x128_1_addressm), .outValue(videocard128x128_1_outvalue[2]));  // open: reset
  // RGB_Video rgb_video_1: pin names not known; wires that end beside it: in_1, clk, 1'b1, videocard128x128_1_x, videocard128x128_1_y, {3{videocard128x128_1_outvalue[2]}}
endmodule

module RegisterKbd (
  input  clk,
  input  [15:0] in16,
  input  load,
  output [15:0] out16
);

  wire and_1_out, clk_read, clk_write;

  and and_1 (and_1_out, load, clk_write);
  Counter #(.max('h1), .width(1)) counter_1 (.Q(clk_read), .clk(clk));  // open: load, D, count, carry, up, clr
  Register #(.width(16)) register_1 (.D(in16), .en(and_1_out), .clk(clk), .Q(out16));  // open: clr
  not not_1 (clk_write, clk_read);

  // Notes on the sheet:
  //   has to be 2x the system clock, this way in "one system cycle" write and read can happen 
  //   ie. the cpu can read the pressed key and the keyboard can set the pressed key at the same time/on the same cycle
endmodule

module MemoryWithIO (
  input  [15:0] in16,
  input  clk_2x,
  input  clk,
  input  load,
  input  [14:0] address15,
  input  [12:0] addressScreen,
  input  loadKbd,
  input  [15:0] inKbd,
  output [15:0] out16,
  output [15:0] outScreen
);

  wire demultiplexer_1_out0, demultiplexer_1_out1;
  wire [15:0] dualportram8k_1_a_out, multiplexer_1_out, ram16kbuiltin_1_out16, registerkbd_1_out16;

  Demultiplexer demultiplexer_1 (
    .out0(demultiplexer_1_out0), .out1(demultiplexer_1_out1), .in(load), .sel(address15[14]));
  RAM16KBuiltIn ram16kbuiltin_1 (
    .load(demultiplexer_1_out0), .address(address15[13:0]), .in16(in16), .clk(clk),
    .out16(ram16kbuiltin_1_out16));
  DualPortRAM8K dualportram8k_1 (
    .load(demultiplexer_1_out1), .a_address(address15[12:0]), .b_address(addressScreen), .clk(clk_2x),
    .in16(in16), .a_out(dualportram8k_1_a_out), .b_out(outScreen));
  RegisterKbd registerkbd_1 (.clk(clk_2x), .load(loadKbd), .in16(inKbd), .out16(registerkbd_1_out16));
  Multiplexer #(.width(16)) multiplexer_1 (
    .in0(dualportram8k_1_a_out), .in1(registerkbd_1_out16), .out(multiplexer_1_out), .sel(address15[13]));
  Multiplexer #(.width(16)) multiplexer_2 (
    .in0(ram16kbuiltin_1_out16), .in1(multiplexer_1_out), .out(out16), .sel(address15[14]));
endmodule

module KBD (
  output [15:0] out_1
);

  wire button_44_out, button_63_out, button_71_out, sysclk, sysclk2x;
  wire [2:0] button_65_out, button_68_out, button_72_out;
  wire [10:0] button_20_out, button_75_out, button_80_out;
  wire [11:0] button_13_out, button_17_out, button_77_out, button_79_out;
  wire [12:0] button_1_out;
  wire [13:0] button_3_out;
  wire [15:0] kbdencoder_1_value;

  Button button_1 (.out(button_1_out[0]));
  Button button_2 (.out(button_1_out[1]));
  Button button_3 (.out(button_3_out[0]));
  Button button_4 (.out(button_3_out[1]));
  Button button_5 (.out(button_1_out[2]));
  Button button_6 (.out(button_1_out[3]));
  Button button_7 (.out(button_1_out[4]));
  Button button_8 (.out(button_1_out[5]));
  Button button_9 (.out(button_3_out[2]));
  Button button_10 (.out(button_3_out[3]));
  Button button_11 (.out(button_3_out[4]));
  Button button_12 (.out(button_3_out[5]));
  Button button_13 (.out(button_13_out[0]));
  Button button_14 (.out(button_13_out[1]));
  Button button_15 (.out(button_13_out[2]));
  Button button_16 (.out(button_13_out[3]));
  Button button_17 (.out(button_17_out[0]));
  Button button_18 (.out(button_17_out[1]));
  Button button_19 (.out(button_17_out[2]));
  Button button_20 (.out(button_20_out[0]));
  Button button_21 (.out(button_20_out[1]));
  Button button_22 (.out(button_20_out[2]));
  Button button_23 (.out(button_20_out[3]));
  Button button_24 (.out(button_1_out[6]));
  Button button_25 (.out(button_1_out[7]));
  Button button_26 (.out(button_1_out[8]));
  Button button_27 (.out(button_1_out[9]));
  Button button_28 (.out(button_3_out[6]));
  Button button_29 (.out(button_3_out[7]));
  Button button_30 (.out(button_3_out[8]));
  Button button_31 (.out(button_3_out[9]));
  Button button_32 (.out(button_13_out[4]));
  Button button_33 (.out(button_13_out[5]));
  Button button_34 (.out(button_13_out[6]));
  Button button_35 (.out(button_13_out[7]));
  Button button_36 (.out(button_17_out[3]));
  Button button_37 (.out(button_17_out[4]));
  Button button_38 (.out(button_17_out[5]));
  Button button_39 (.out(button_17_out[6]));
  Button button_40 (.out(button_20_out[4]));
  Button button_41 (.out(button_20_out[5]));
  Button button_42 (.out(button_20_out[6]));
  Button button_43 (.out(button_20_out[7]));
  Button button_44 (.out(button_44_out));
  Button button_45 (.out(button_1_out[10]));
  Button button_46 (.out(button_1_out[11]));
  Button button_47 (.out(button_1_out[12]));
  Button button_48 (.out(button_3_out[10]));
  Button button_49 (.out(button_3_out[11]));
  Button button_50 (.out(button_3_out[12]));
  Button button_51 (.out(button_3_out[13]));
  Button button_52 (.out(button_13_out[8]));
  Button button_53 (.out(button_13_out[9]));
  Button button_54 (.out(button_13_out[10]));
  Button button_55 (.out(button_13_out[11]));
  Button button_56 (.out(button_17_out[7]));
  Button button_57 (.out(button_17_out[8]));
  Button button_58 (.out(button_17_out[9]));
  Button button_59 (.out(button_17_out[10]));
  Button button_60 (.out(button_20_out[8]));
  Button button_61 (.out(button_20_out[9]));
  Button button_62 (.out(button_20_out[10]));
  KBDEncoder kbdencoder_1 (
    .qtoClosingbracket(button_13_out), .bactick2backspace(button_3_out), .esc2f12(button_1_out),
    .space(button_44_out), .enter(button_63_out), .ins2pgup(button_65_out), .del2pgdwn(button_68_out),
    .up(button_71_out), .Backslash2Slash(button_20_out), .lt2rt(button_72_out), .verbar2qstn(button_80_out),
    .A2Tilde(button_79_out), .Q2closingcurly(button_77_out), .excl2plus(button_75_out),
    .a2hashtag(button_17_out), .value(kbdencoder_1_value));
  Button button_63 (.out(button_63_out));
  Button button_64 (.out(button_17_out[11]));
  Button button_65 (.out(button_65_out[0]));
  Button button_66 (.out(button_65_out[1]));
  Button button_67 (.out(button_65_out[2]));
  Button button_68 (.out(button_68_out[0]));
  Button button_69 (.out(button_68_out[1]));
  Button button_70 (.out(button_68_out[2]));
  Button button_71 (.out(button_71_out));
  Button button_72 (.out(button_72_out[0]));
  Button button_73 (.out(button_72_out[1]));
  Button button_74 (.out(button_72_out[2]));
  Clock clock_1 (.out(sysclk2x));
  Button button_75 (.out(button_75_out[0]));
  Button button_76 (.out(button_75_out[1]));
  Button button_77 (.out(button_77_out[0]));
  Button button_78 (.out(button_77_out[1]));
  Button button_79 (.out(button_79_out[0]));
  Button button_80 (.out(button_80_out[0]));
  Button button_81 (.out(button_80_out[1]));
  Counter #(.max('h1), .width(1)) counter_1 (.Q(sysclk), .clk(sysclk2x));  // open: load, D, count, carry, up, clr
  Button button_82 (.out(button_75_out[2]));
  Button button_83 (.out(button_75_out[3]));
  Button button_84 (.out(button_75_out[4]));
  Button button_85 (.out(button_75_out[5]));
  Button button_86 (.out(button_77_out[2]));
  Button button_87 (.out(button_77_out[3]));
  Button button_88 (.out(button_77_out[4]));
  Button button_89 (.out(button_77_out[5]));
  Button button_90 (.out(button_79_out[1]));
  Button button_91 (.out(button_79_out[2]));
  Button button_92 (.out(button_79_out[3]));
  Button button_93 (.out(button_79_out[4]));
  Button button_94 (.out(button_80_out[2]));
  Button button_95 (.out(button_80_out[3]));
  Button button_96 (.out(button_80_out[4]));
  Button button_97 (.out(button_80_out[5]));
  MemoryWithIO memorywithio_1 (
    .address15(15'h6000), .loadKbd(1'b1), .clk_2x(sysclk2x), .inKbd(kbdencoder_1_value), .clk(sysclk),
    .out16(out_1));  // open: load, in16, addressScreen, outScreen
  Button button_98 (.out(button_75_out[6]));
  Button button_99 (.out(button_75_out[7]));
  Button button_100 (.out(button_75_out[8]));
  Button button_101 (.out(button_75_out[9]));
  Button button_102 (.out(button_77_out[6]));
  Button button_103 (.out(button_77_out[7]));
  Button button_104 (.out(button_77_out[8]));
  Button button_105 (.out(button_77_out[9]));
  Button button_106 (.out(button_79_out[5]));
  Button button_107 (.out(button_79_out[6]));
  Button button_108 (.out(button_79_out[7]));
  Button button_109 (.out(button_79_out[8]));
  Button button_110 (.out(button_80_out[6]));
  Button button_111 (.out(button_80_out[7]));
  Button button_112 (.out(button_80_out[8]));
  Button button_113 (.out(button_80_out[9]));
  Button button_114 (.out(button_75_out[10]));
  Button button_115 (.out(button_77_out[10]));
  Button button_116 (.out(button_77_out[11]));
  Button button_117 (.out(button_79_out[9]));
  Button button_118 (.out(button_79_out[10]));
  Button button_119 (.out(button_79_out[11]));
  Button button_120 (.out(button_80_out[10]));

  // Notes on the sheet:
  //   esc
  //   f1
  //   `
  //   1
  //   f2
  //   f3
  //   f4
  //   f5
  //   2
  //   3
  //   4
  //   5
  //   q
  //   w
  //   e
  //   r
  //   a
  //   s
  //   d
  //   f
  //   \
  //   z
  //   x
  //   c
  //   f6
  //   f7
  //   f8
  //   f9
  //   6
  //   7
  //   8
  //   9
  //   t
  //   y
  //   u
  //   i
  //   g
  //   h
  //   j
  //   v
  //   b
  //   n
  //   m
  //   sp
  //   f10
  //   f11
  //   f12
  //   0
  //   -
  //   =
  //   bsp
  //   p
  //   o
  //   [
  //   ]
  //   k
  //   l
  //   ;
  //   '
  //   #
  //   ,
  //   .
  //   /
  //   ins
  //   del
  //   ent
  //   hme
  //   pgu
  //   end
  //   pgd
  //   up
  //   lt
  //   dn
  //   rt
  //   !
  //   "
  //   $
  //   Q
  //   W
  //   A
  //   S
  //   |
  //   Z
  //   %
  //   ^
  //   &
  //   *
  //   E
  //   R
  //   T
  //   Y
  //   D
  //   F
  //   G
  //   H
  //   X
  //   C
  //   V
  //   B
  //   _
  //   (
  //   )
  //   U
  //   I
  //   O
  //   P
  //   J
  //   K
  //   L
  //   :
  //   N
  //   M
  //   <
  //   >
  //   +
  //   {
  //   }
  //   @
  //   ~
  //   ?
endmodule

module KBDEncoder (
  input  [10:0] Backslash2Slash,
  input  [11:0] a2hashtag,
  input  [11:0] qtoClosingbracket,
  input  [13:0] bactick2backspace,
  input  [12:0] esc2f12,
  input  [10:0] verbar2qstn,
  input  [11:0] A2Tilde,
  input  [11:0] Q2closingcurly,
  input  [2:0] ins2pgup,
  input  [2:0] del2pgdwn,
  input  [2:0] lt2rt,
  input  [10:0] excl2plus,
  input  space,
  input  enter,
  input  up,
  output [15:0] value
);

  wire [15:0] multiplexer_1_out, multiplexer_2_out, multiplexer_3_out, multiplexer_4_out, multiplexer_5_out,
       multiplexer_6_out, multiplexer_7_out, multiplexer_8_out, multiplexer_9_out, multiplexer_10_out,
       multiplexer_11_out, multiplexer_12_out, multiplexer_13_out, multiplexer_14_out, multiplexer_15_out,
       multiplexer_16_out, multiplexer_17_out, multiplexer_18_out, multiplexer_19_out, multiplexer_20_out,
       multiplexer_21_out, multiplexer_22_out, multiplexer_23_out, multiplexer_24_out, multiplexer_25_out,
       multiplexer_26_out, multiplexer_27_out, multiplexer_28_out, multiplexer_29_out, multiplexer_30_out,
       multiplexer_31_out, multiplexer_32_out, multiplexer_33_out, multiplexer_34_out, multiplexer_35_out,
       multiplexer_36_out, multiplexer_37_out, multiplexer_38_out, multiplexer_39_out, multiplexer_40_out,
       multiplexer_41_out, multiplexer_42_out, multiplexer_43_out, multiplexer_44_out, multiplexer_45_out,
       multiplexer_46_out, multiplexer_47_out, multiplexer_48_out, multiplexer_49_out, multiplexer_50_out,
       multiplexer_51_out, multiplexer_52_out, multiplexer_53_out, multiplexer_54_out, multiplexer_55_out,
       multiplexer_56_out, multiplexer_57_out, multiplexer_58_out, multiplexer_59_out, multiplexer_60_out,
       multiplexer_61_out, multiplexer_62_out, multiplexer_63_out, multiplexer_64_out, multiplexer_65_out,
       multiplexer_66_out, multiplexer_67_out, multiplexer_68_out, multiplexer_69_out, multiplexer_70_out,
       multiplexer_71_out, multiplexer_72_out, multiplexer_73_out, multiplexer_74_out, multiplexer_75_out,
       multiplexer_76_out, multiplexer_77_out, multiplexer_78_out, multiplexer_79_out, multiplexer_80_out,
       multiplexer_81_out, multiplexer_82_out, multiplexer_83_out, multiplexer_84_out, multiplexer_85_out,
       multiplexer_86_out, multiplexer_87_out, multiplexer_88_out, multiplexer_89_out, multiplexer_90_out,
       multiplexer_91_out, multiplexer_92_out, multiplexer_93_out, multiplexer_94_out, multiplexer_95_out,
       multiplexer_96_out, multiplexer_97_out, multiplexer_98_out, multiplexer_99_out, multiplexer_100_out,
       multiplexer_101_out, multiplexer_102_out, multiplexer_103_out, multiplexer_104_out,
       multiplexer_105_out, multiplexer_106_out, multiplexer_107_out, multiplexer_108_out,
       multiplexer_109_out, multiplexer_110_out, multiplexer_111_out, multiplexer_112_out,
       multiplexer_113_out, multiplexer_114_out, multiplexer_115_out, multiplexer_116_out,
       multiplexer_117_out, multiplexer_118_out, multiplexer_119_out, multiplexer_120_out, or_1_out,
       or_2_out, or_3_out, or_4_out, or_6_out, or_7_out, or_8_out, or_9_out, or_10_out, or_11_out, or_12_out,
       or_13_out;

  Multiplexer #(.width(16)) multiplexer_1 (
    .in0({16{1'b0}}), .in1(16'h5c), .out(multiplexer_1_out), .sel(Backslash2Slash[0]));
  Multiplexer #(.width(16)) multiplexer_2 (
    .in0({16{1'b0}}), .in1(16'h7a), .out(multiplexer_2_out), .sel(Backslash2Slash[1]));
  Multiplexer #(.width(16)) multiplexer_3 (
    .in0({16{1'b0}}), .in1(16'h78), .out(multiplexer_3_out), .sel(Backslash2Slash[2]));
  Multiplexer #(.width(16)) multiplexer_4 (
    .in0({16{1'b0}}), .in1(16'h63), .out(multiplexer_4_out), .sel(Backslash2Slash[3]));
  assign or_1_out = multiplexer_1_out | multiplexer_2_out | multiplexer_3_out | multiplexer_4_out | multiplexer_5_out | multiplexer_6_out | multiplexer_7_out | multiplexer_8_out | multiplexer_9_out | multiplexer_10_out | multiplexer_11_out;  // OR_Gate or_1, 16 bits wide
  Multiplexer #(.width(16)) multiplexer_5 (
    .in0({16{1'b0}}), .in1(16'h76), .out(multiplexer_5_out), .sel(Backslash2Slash[4]));
  Multiplexer #(.width(16)) multiplexer_6 (
    .in0({16{1'b0}}), .in1(16'h62), .out(multiplexer_6_out), .sel(Backslash2Slash[5]));
  Multiplexer #(.width(16)) multiplexer_7 (
    .in0({16{1'b0}}), .in1(16'h6e), .out(multiplexer_7_out), .sel(Backslash2Slash[6]));
  Multiplexer #(.width(16)) multiplexer_8 (
    .in0({16{1'b0}}), .in1(16'h6d), .out(multiplexer_8_out), .sel(Backslash2Slash[7]));
  Multiplexer #(.width(16)) multiplexer_9 (
    .in0({16{1'b0}}), .in1(16'h2c), .out(multiplexer_9_out), .sel(Backslash2Slash[8]));
  Multiplexer #(.width(16)) multiplexer_10 (
    .in0({16{1'b0}}), .in1(16'h2e), .out(multiplexer_10_out), .sel(Backslash2Slash[9]));
  Multiplexer #(.width(16)) multiplexer_11 (
    .in0({16{1'b0}}), .in1(16'h2f), .out(multiplexer_11_out), .sel(Backslash2Slash[10]));
  Multiplexer #(.width(16)) multiplexer_12 (
    .in0({16{1'b0}}), .in1(16'h61), .out(multiplexer_12_out), .sel(a2hashtag[0]));
  Multiplexer #(.width(16)) multiplexer_13 (
    .in0({16{1'b0}}), .in1(16'h73), .out(multiplexer_13_out), .sel(a2hashtag[1]));
  Multiplexer #(.width(16)) multiplexer_14 (
    .in0({16{1'b0}}), .in1(16'h64), .out(multiplexer_14_out), .sel(a2hashtag[2]));
  Multiplexer #(.width(16)) multiplexer_15 (
    .in0({16{1'b0}}), .in1(16'h66), .out(multiplexer_15_out), .sel(a2hashtag[3]));
  Multiplexer #(.width(16)) multiplexer_16 (
    .in0({16{1'b0}}), .in1(16'h67), .out(multiplexer_16_out), .sel(a2hashtag[4]));
  assign or_2_out = multiplexer_12_out | multiplexer_13_out | multiplexer_14_out | multiplexer_15_out | multiplexer_16_out | multiplexer_17_out | multiplexer_18_out | multiplexer_20_out | multiplexer_19_out | multiplexer_21_out | multiplexer_22_out | multiplexer_23_out;  // OR_Gate or_2, 16 bits wide
  Multiplexer #(.width(16)) multiplexer_17 (
    .in0({16{1'b0}}), .in1(16'h68), .out(multiplexer_17_out), .sel(a2hashtag[5]));
  Multiplexer #(.width(16)) multiplexer_18 (
    .in0({16{1'b0}}), .in1(16'h6a), .out(multiplexer_18_out), .sel(a2hashtag[6]));
  Multiplexer #(.width(16)) multiplexer_19 (
    .in0({16{1'b0}}), .in1(16'h6c), .out(multiplexer_19_out), .sel(a2hashtag[8]));
  Multiplexer #(.width(16)) multiplexer_20 (
    .in0({16{1'b0}}), .in1(16'h6b), .out(multiplexer_20_out), .sel(a2hashtag[7]));
  Multiplexer #(.width(16)) multiplexer_21 (
    .in0({16{1'b0}}), .in1(16'h3b), .out(multiplexer_21_out), .sel(a2hashtag[9]));
  Multiplexer #(.width(16)) multiplexer_22 (
    .in0({16{1'b0}}), .in1(16'h27), .out(multiplexer_22_out), .sel(a2hashtag[10]));
  Multiplexer #(.width(16)) multiplexer_23 (
    .in0({16{1'b0}}), .in1(16'h23), .out(multiplexer_23_out), .sel(a2hashtag[11]));
  Multiplexer #(.width(16)) multiplexer_24 (
    .in0({16{1'b0}}), .in1(16'h71), .out(multiplexer_24_out), .sel(qtoClosingbracket[0]));
  Multiplexer #(.width(16)) multiplexer_25 (
    .in0({16{1'b0}}), .in1(16'h77), .out(multiplexer_25_out), .sel(qtoClosingbracket[1]));
  Multiplexer #(.width(16)) multiplexer_26 (
    .in0({16{1'b0}}), .in1(16'h65), .out(multiplexer_26_out), .sel(qtoClosingbracket[2]));
  Multiplexer #(.width(16)) multiplexer_27 (
    .in0({16{1'b0}}), .in1(16'h72), .out(multiplexer_27_out), .sel(qtoClosingbracket[3]));
  assign or_3_out = multiplexer_24_out | multiplexer_25_out | multiplexer_26_out | multiplexer_27_out | multiplexer_28_out | multiplexer_29_out | multiplexer_30_out | multiplexer_31_out | multiplexer_32_out | multiplexer_33_out | multiplexer_34_out | multiplexer_35_out;  // OR_Gate or_3, 16 bits wide
  Multiplexer #(.width(16)) multiplexer_28 (
    .in0({16{1'b0}}), .in1(16'h74), .out(multiplexer_28_out), .sel(qtoClosingbracket[4]));
  Multiplexer #(.width(16)) multiplexer_29 (
    .in0({16{1'b0}}), .in1(16'h79), .out(multiplexer_29_out), .sel(qtoClosingbracket[5]));
  Multiplexer #(.width(16)) multiplexer_30 (
    .in0({16{1'b0}}), .in1(16'h75), .out(multiplexer_30_out), .sel(qtoClosingbracket[6]));
  Multiplexer #(.width(16)) multiplexer_31 (
    .in0({16{1'b0}}), .in1(16'h69), .out(multiplexer_31_out), .sel(qtoClosingbracket[7]));
  Multiplexer #(.width(16)) multiplexer_32 (
    .in0({16{1'b0}}), .in1(16'h6f), .out(multiplexer_32_out), .sel(qtoClosingbracket[8]));
  Multiplexer #(.width(16)) multiplexer_33 (
    .in0({16{1'b0}}), .in1(16'h70), .out(multiplexer_33_out), .sel(qtoClosingbracket[9]));
  Multiplexer #(.width(16)) multiplexer_34 (
    .in0({16{1'b0}}), .in1(16'h5b), .out(multiplexer_34_out), .sel(qtoClosingbracket[10]));
  Multiplexer #(.width(16)) multiplexer_35 (
    .in0({16{1'b0}}), .in1(16'h5d), .out(multiplexer_35_out), .sel(qtoClosingbracket[11]));
  Multiplexer #(.width(16)) multiplexer_36 (
    .in0({16{1'b0}}), .in1(16'h60), .out(multiplexer_36_out), .sel(bactick2backspace[0]));
  Multiplexer #(.width(16)) multiplexer_37 (
    .in0({16{1'b0}}), .in1(16'h31), .out(multiplexer_37_out), .sel(bactick2backspace[1]));
  Multiplexer #(.width(16)) multiplexer_38 (
    .in0({16{1'b0}}), .in1(16'h32), .out(multiplexer_38_out), .sel(bactick2backspace[2]));
  Multiplexer #(.width(16)) multiplexer_39 (
    .in0({16{1'b0}}), .in1(16'h33), .out(multiplexer_39_out), .sel(bactick2backspace[3]));
  Multiplexer #(.width(16)) multiplexer_40 (
    .in0({16{1'b0}}), .in1(16'h34), .out(multiplexer_40_out), .sel(bactick2backspace[4]));
  Multiplexer #(.width(16)) multiplexer_41 (
    .in0({16{1'b0}}), .in1(16'h35), .out(multiplexer_41_out), .sel(bactick2backspace[5]));
  Multiplexer #(.width(16)) multiplexer_42 (
    .in0({16{1'b0}}), .in1(16'h36), .out(multiplexer_42_out), .sel(bactick2backspace[6]));
  assign or_4_out = multiplexer_36_out | multiplexer_37_out | multiplexer_38_out | multiplexer_39_out | multiplexer_40_out | multiplexer_41_out | multiplexer_42_out | multiplexer_43_out | multiplexer_44_out | multiplexer_45_out | multiplexer_46_out | multiplexer_47_out | multiplexer_48_out | multiplexer_49_out;  // OR_Gate or_4, 16 bits wide
  Multiplexer #(.width(16)) multiplexer_43 (
    .in0({16{1'b0}}), .in1(16'h37), .out(multiplexer_43_out), .sel(bactick2backspace[7]));
  Multiplexer #(.width(16)) multiplexer_44 (
    .in0({16{1'b0}}), .in1(16'h38), .out(multiplexer_44_out), .sel(bactick2backspace[8]));
  Multiplexer #(.width(16)) multiplexer_45 (
    .in0({16{1'b0}}), .in1(16'h39), .out(multiplexer_45_out), .sel(bactick2backspace[9]));
  Multiplexer #(.width(16)) multiplexer_46 (
    .in0({16{1'b0}}), .in1(16'h30), .out(multiplexer_46_out), .sel(bactick2backspace[10]));
  Multiplexer #(.width(16)) multiplexer_47 (
    .in0({16{1'b0}}), .in1(16'h2d), .out(multiplexer_47_out), .sel(bactick2backspace[11]));
  Multiplexer #(.width(16)) multiplexer_48 (
    .in0({16{1'b0}}), .in1(16'h3d), .out(multiplexer_48_out), .sel(bactick2backspace[12]));
  Multiplexer #(.width(16)) multiplexer_49 (
    .in0({16{1'b0}}), .in1(16'h81), .out(multiplexer_49_out), .sel(bactick2backspace[13]));
  assign value = or_1_out | or_2_out | or_3_out | or_4_out | or_6_out | multiplexer_63_out | multiplexer_64_out | or_7_out | or_8_out | multiplexer_71_out | or_9_out | or_10_out | or_11_out | or_12_out | or_13_out;  // OR_Gate or_5, 16 bits wide
  Multiplexer #(.width(16)) multiplexer_50 (.in0({16{1'b0}}), .in1(16'h8c), .out(multiplexer_50_out), .sel(esc2f12[0]));
  Multiplexer #(.width(16)) multiplexer_51 (.in0({16{1'b0}}), .in1(16'h8d), .out(multiplexer_51_out), .sel(esc2f12[1]));
  Multiplexer #(.width(16)) multiplexer_52 (.in0({16{1'b0}}), .in1(16'h8e), .out(multiplexer_52_out), .sel(esc2f12[2]));
  Multiplexer #(.width(16)) multiplexer_53 (.in0({16{1'b0}}), .in1(16'h8f), .out(multiplexer_53_out), .sel(esc2f12[3]));
  Multiplexer #(.width(16)) multiplexer_54 (.in0({16{1'b0}}), .in1(16'h90), .out(multiplexer_54_out), .sel(esc2f12[4]));
  Multiplexer #(.width(16)) multiplexer_55 (.in0({16{1'b0}}), .in1(16'h91), .out(multiplexer_55_out), .sel(esc2f12[5]));
  assign or_6_out = multiplexer_50_out | multiplexer_51_out | multiplexer_52_out | multiplexer_53_out | multiplexer_54_out | multiplexer_55_out | multiplexer_56_out | multiplexer_57_out | multiplexer_58_out | multiplexer_59_out | multiplexer_60_out | multiplexer_61_out | multiplexer_62_out;  // OR_Gate or_6, 16 bits wide
  Multiplexer #(.width(16)) multiplexer_56 (.in0({16{1'b0}}), .in1(16'h92), .out(multiplexer_56_out), .sel(esc2f12[6]));
  Multiplexer #(.width(16)) multiplexer_57 (.in0({16{1'b0}}), .in1(16'h93), .out(multiplexer_57_out), .sel(esc2f12[7]));
  Multiplexer #(.width(16)) multiplexer_58 (.in0({16{1'b0}}), .in1(16'h94), .out(multiplexer_58_out), .sel(esc2f12[8]));
  Multiplexer #(.width(16)) multiplexer_59 (.in0({16{1'b0}}), .in1(16'h95), .out(multiplexer_59_out), .sel(esc2f12[9]));
  Multiplexer #(.width(16)) multiplexer_60 (
    .in0({16{1'b0}}), .in1(16'h96), .out(multiplexer_60_out), .sel(esc2f12[10]));
  Multiplexer #(.width(16)) multiplexer_61 (
    .in0({16{1'b0}}), .in1(16'h97), .out(multiplexer_61_out), .sel(esc2f12[11]));
  Multiplexer #(.width(16)) multiplexer_62 (
    .in0({16{1'b0}}), .in1(16'h98), .out(multiplexer_62_out), .sel(esc2f12[12]));
  Multiplexer #(.width(16)) multiplexer_63 (.in0({16{1'b0}}), .in1(16'h20), .out(multiplexer_63_out), .sel(space));
  Multiplexer #(.width(16)) multiplexer_64 (.in0({16{1'b0}}), .in1(16'h80), .out(multiplexer_64_out), .sel(enter));
  Multiplexer #(.width(16)) multiplexer_65 (
    .in0({16{1'b0}}), .in1(16'h8a), .out(multiplexer_65_out), .sel(ins2pgup[0]));
  assign or_7_out = multiplexer_65_out | multiplexer_66_out | multiplexer_67_out;  // OR_Gate or_7, 16 bits wide
  Multiplexer #(.width(16)) multiplexer_66 (
    .in0({16{1'b0}}), .in1(16'h86), .out(multiplexer_66_out), .sel(ins2pgup[1]));
  Multiplexer #(.width(16)) multiplexer_67 (
    .in0({16{1'b0}}), .in1(16'h88), .out(multiplexer_67_out), .sel(ins2pgup[2]));
  Multiplexer #(.width(16)) multiplexer_68 (
    .in0({16{1'b0}}), .in1(16'h8b), .out(multiplexer_68_out), .sel(del2pgdwn[0]));
  assign or_8_out = multiplexer_68_out | multiplexer_69_out | multiplexer_70_out;  // OR_Gate or_8, 16 bits wide
  Multiplexer #(.width(16)) multiplexer_69 (
    .in0({16{1'b0}}), .in1(16'h87), .out(multiplexer_69_out), .sel(del2pgdwn[1]));
  Multiplexer #(.width(16)) multiplexer_70 (
    .in0({16{1'b0}}), .in1(16'h89), .out(multiplexer_70_out), .sel(del2pgdwn[2]));
  Multiplexer #(.width(16)) multiplexer_71 (.in0({16{1'b0}}), .in1(16'h83), .out(multiplexer_71_out), .sel(up));
  Multiplexer #(.width(16)) multiplexer_72 (.in0({16{1'b0}}), .in1(16'h82), .out(multiplexer_72_out), .sel(lt2rt[0]));
  assign or_9_out = multiplexer_72_out | multiplexer_73_out | multiplexer_74_out;  // OR_Gate or_9, 16 bits wide
  Multiplexer #(.width(16)) multiplexer_73 (.in0({16{1'b0}}), .in1(16'h85), .out(multiplexer_73_out), .sel(lt2rt[1]));
  Multiplexer #(.width(16)) multiplexer_74 (.in0({16{1'b0}}), .in1(16'h84), .out(multiplexer_74_out), .sel(lt2rt[2]));
  Multiplexer #(.width(16)) multiplexer_75 (
    .in0({16{1'b0}}), .in1(16'h7c), .out(multiplexer_75_out), .sel(verbar2qstn[0]));
  Multiplexer #(.width(16)) multiplexer_76 (
    .in0({16{1'b0}}), .in1(16'h5a), .out(multiplexer_76_out), .sel(verbar2qstn[1]));
  Multiplexer #(.width(16)) multiplexer_77 (
    .in0({16{1'b0}}), .in1(16'h58), .out(multiplexer_77_out), .sel(verbar2qstn[2]));
  Multiplexer #(.width(16)) multiplexer_78 (
    .in0({16{1'b0}}), .in1(16'h43), .out(multiplexer_78_out), .sel(verbar2qstn[3]));
  Multiplexer #(.width(16)) multiplexer_79 (
    .in0({16{1'b0}}), .in1(16'h56), .out(multiplexer_79_out), .sel(verbar2qstn[4]));
  assign or_10_out = multiplexer_75_out | multiplexer_76_out | multiplexer_77_out | multiplexer_78_out | multiplexer_79_out | multiplexer_80_out | multiplexer_81_out | multiplexer_82_out | multiplexer_83_out | multiplexer_84_out | multiplexer_85_out;  // OR_Gate or_10, 16 bits wide
  Multiplexer #(.width(16)) multiplexer_80 (
    .in0({16{1'b0}}), .in1(16'h42), .out(multiplexer_80_out), .sel(verbar2qstn[5]));
  Multiplexer #(.width(16)) multiplexer_81 (
    .in0({16{1'b0}}), .in1(16'h4e), .out(multiplexer_81_out), .sel(verbar2qstn[6]));
  Multiplexer #(.width(16)) multiplexer_82 (
    .in0({16{1'b0}}), .in1(16'h4d), .out(multiplexer_82_out), .sel(verbar2qstn[7]));
  Multiplexer #(.width(16)) multiplexer_83 (
    .in0({16{1'b0}}), .in1(16'h3c), .out(multiplexer_83_out), .sel(verbar2qstn[8]));
  Multiplexer #(.width(16)) multiplexer_84 (
    .in0({16{1'b0}}), .in1(16'h3e), .out(multiplexer_84_out), .sel(verbar2qstn[9]));
  Multiplexer #(.width(16)) multiplexer_85 (
    .in0({16{1'b0}}), .in1(16'h3f), .out(multiplexer_85_out), .sel(verbar2qstn[10]));
  Multiplexer #(.width(16)) multiplexer_86 (.in0({16{1'b0}}), .in1(16'h41), .out(multiplexer_86_out), .sel(A2Tilde[0]));
  Multiplexer #(.width(16)) multiplexer_87 (.in0({16{1'b0}}), .in1(16'h53), .out(multiplexer_87_out), .sel(A2Tilde[1]));
  Multiplexer #(.width(16)) multiplexer_88 (.in0({16{1'b0}}), .in1(16'h44), .out(multiplexer_88_out), .sel(A2Tilde[2]));
  Multiplexer #(.width(16)) multiplexer_89 (.in0({16{1'b0}}), .in1(16'h46), .out(multiplexer_89_out), .sel(A2Tilde[3]));
  assign or_11_out = multiplexer_86_out | multiplexer_87_out | multiplexer_88_out | multiplexer_89_out | multiplexer_90_out | multiplexer_91_out | multiplexer_92_out | multiplexer_93_out | multiplexer_94_out | multiplexer_95_out | multiplexer_96_out | multiplexer_97_out;  // OR_Gate or_11, 16 bits wide
  Multiplexer #(.width(16)) multiplexer_90 (.in0({16{1'b0}}), .in1(16'h47), .out(multiplexer_90_out), .sel(A2Tilde[4]));
  Multiplexer #(.width(16)) multiplexer_91 (.in0({16{1'b0}}), .in1(16'h48), .out(multiplexer_91_out), .sel(A2Tilde[5]));
  Multiplexer #(.width(16)) multiplexer_92 (.in0({16{1'b0}}), .in1(16'h4a), .out(multiplexer_92_out), .sel(A2Tilde[6]));
  Multiplexer #(.width(16)) multiplexer_93 (.in0({16{1'b0}}), .in1(16'h4b), .out(multiplexer_93_out), .sel(A2Tilde[7]));
  Multiplexer #(.width(16)) multiplexer_94 (.in0({16{1'b0}}), .in1(16'h4c), .out(multiplexer_94_out), .sel(A2Tilde[8]));
  Multiplexer #(.width(16)) multiplexer_95 (.in0({16{1'b0}}), .in1(16'h3a), .out(multiplexer_95_out), .sel(A2Tilde[9]));
  Multiplexer #(.width(16)) multiplexer_96 (
    .in0({16{1'b0}}), .in1(16'h40), .out(multiplexer_96_out), .sel(A2Tilde[10]));
  Multiplexer #(.width(16)) multiplexer_97 (
    .in0({16{1'b0}}), .in1(16'h7e), .out(multiplexer_97_out), .sel(A2Tilde[11]));
  Multiplexer #(.width(16)) multiplexer_98 (
    .in0({16{1'b0}}), .in1(16'h51), .out(multiplexer_98_out), .sel(Q2closingcurly[0]));
  Multiplexer #(.width(16)) multiplexer_99 (
    .in0({16{1'b0}}), .in1(16'h57), .out(multiplexer_99_out), .sel(Q2closingcurly[1]));
  Multiplexer #(.width(16)) multiplexer_100 (
    .in0({16{1'b0}}), .in1(16'h45), .out(multiplexer_100_out), .sel(Q2closingcurly[2]));
  Multiplexer #(.width(16)) multiplexer_101 (
    .in0({16{1'b0}}), .in1(16'h52), .out(multiplexer_101_out), .sel(Q2closingcurly[3]));
  assign or_12_out = multiplexer_98_out | multiplexer_99_out | multiplexer_100_out | multiplexer_101_out | multiplexer_102_out | multiplexer_103_out | multiplexer_104_out | multiplexer_105_out | multiplexer_106_out | multiplexer_107_out | multiplexer_108_out | multiplexer_109_out;  // OR_Gate or_12, 16 bits wide
  Multiplexer #(.width(16)) multiplexer_102 (
    .in0({16{1'b0}}), .in1(16'h54), .out(multiplexer_102_out), .sel(Q2closingcurly[4]));
  Multiplexer #(.width(16)) multiplexer_103 (
    .in0({16{1'b0}}), .in1(16'h59), .out(multiplexer_103_out), .sel(Q2closingcurly[5]));
  Multiplexer #(.width(16)) multiplexer_104 (
    .in0({16{1'b0}}), .in1(16'h55), .out(multiplexer_104_out), .sel(Q2closingcurly[6]));
  Multiplexer #(.width(16)) multiplexer_105 (
    .in0({16{1'b0}}), .in1(16'h49), .out(multiplexer_105_out), .sel(Q2closingcurly[7]));
  Multiplexer #(.width(16)) multiplexer_106 (
    .in0({16{1'b0}}), .in1(16'h4f), .out(multiplexer_106_out), .sel(Q2closingcurly[8]));
  Multiplexer #(.width(16)) multiplexer_107 (
    .in0({16{1'b0}}), .in1(16'h50), .out(multiplexer_107_out), .sel(Q2closingcurly[9]));
  Multiplexer #(.width(16)) multiplexer_108 (
    .in0({16{1'b0}}), .in1(16'h7b), .out(multiplexer_108_out), .sel(Q2closingcurly[10]));
  Multiplexer #(.width(16)) multiplexer_109 (
    .in0({16{1'b0}}), .in1(16'h7d), .out(multiplexer_109_out), .sel(Q2closingcurly[11]));
  Multiplexer #(.width(16)) multiplexer_110 (
    .in0({16{1'b0}}), .in1(16'h21), .out(multiplexer_110_out), .sel(excl2plus[0]));
  Multiplexer #(.width(16)) multiplexer_111 (
    .in0({16{1'b0}}), .in1(16'h22), .out(multiplexer_111_out), .sel(excl2plus[1]));
  Multiplexer #(.width(16)) multiplexer_112 (
    .in0({16{1'b0}}), .in1(16'h24), .out(multiplexer_112_out), .sel(excl2plus[2]));
  Multiplexer #(.width(16)) multiplexer_113 (
    .in0({16{1'b0}}), .in1(16'h25), .out(multiplexer_113_out), .sel(excl2plus[3]));
  Multiplexer #(.width(16)) multiplexer_114 (
    .in0({16{1'b0}}), .in1(16'h5e), .out(multiplexer_114_out), .sel(excl2plus[4]));
  assign or_13_out = multiplexer_110_out | multiplexer_111_out | multiplexer_112_out | multiplexer_113_out | multiplexer_114_out | multiplexer_115_out | multiplexer_116_out | multiplexer_117_out | multiplexer_118_out | multiplexer_119_out | multiplexer_120_out;  // OR_Gate or_13, 16 bits wide
  Multiplexer #(.width(16)) multiplexer_115 (
    .in0({16{1'b0}}), .in1(16'h26), .out(multiplexer_115_out), .sel(excl2plus[5]));
  Multiplexer #(.width(16)) multiplexer_116 (
    .in0({16{1'b0}}), .in1(16'h2a), .out(multiplexer_116_out), .sel(excl2plus[6]));
  Multiplexer #(.width(16)) multiplexer_117 (
    .in0({16{1'b0}}), .in1(16'h28), .out(multiplexer_117_out), .sel(excl2plus[7]));
  Multiplexer #(.width(16)) multiplexer_118 (
    .in0({16{1'b0}}), .in1(16'h29), .out(multiplexer_118_out), .sel(excl2plus[8]));
  Multiplexer #(.width(16)) multiplexer_119 (
    .in0({16{1'b0}}), .in1(16'h5f), .out(multiplexer_119_out), .sel(excl2plus[9]));
  Multiplexer #(.width(16)) multiplexer_120 (
    .in0({16{1'b0}}), .in1(16'h2b), .out(multiplexer_120_out), .sel(excl2plus[10]));
endmodule

module CPU (
  input  [15:0] instruction,
  input  [15:0] inM,
  input  reset,
  input  clk,
  output [15:0] outM,
  output writeM,
  output [14:0] addressM,
  output [14:0] programcounter
);

  wire and_3_out, and_11_out, and_12_out, and_13_out, and_14_out, and_15_out, and_16_out, EQ, GE, GT, isA,
       JEQ, JGE, JGT, JLE, JLT, JMP, JNE, JUMP, LE, LT, nand_1_out, NE, ng, not_2_out, not_3_out, not_4_out,
       not_5_out, not_7_out, not_8_out, not_9_out, not_10_out, not_11_out, not_12_out, not_13_out,
       not_14_out, not_15_out, or_1_out, or_4_out;
  wire [15:0] multiplexer_1_out, multiplexer_2_out, register16_2_out16;
  wire [15:15] pc_1_out16, register16_1_out16;

  Multiplexer #(.width(16)) multiplexer_1 (.in0(outM), .in1(instruction), .out(multiplexer_1_out), .sel(nand_1_out));
  nand nand_1 (nand_1_out, instruction[15], instruction[5]);
  not not_1 (isA, instruction[15]);
  or or_1 (or_1_out, isA, instruction[5]);
  Register16 register16_1 (
    .in16(multiplexer_1_out), .clk(clk), .load(or_1_out), .out16({register16_1_out16[15], addressM}));
  not not_2 (not_2_out, EQ);
  not not_3 (not_3_out, ng);
  not not_4 (not_4_out, ng);
  not not_5 (not_5_out, EQ);
  Multiplexer #(.width(16)) multiplexer_2 (
    .in0({register16_1_out16[15], addressM}), .in1(inM), .out(multiplexer_2_out), .sel(instruction[12]));
  and and_1 (GT, not_2_out, not_3_out);
  or or_2 (GE, EQ, not_4_out);
  and and_2 (LT, not_5_out, ng);
  not not_6 (NE, EQ);
  or or_3 (LE, EQ, ng);
  and and_3 (and_3_out, instruction[15], instruction[4]);
  Register16 register16_2 (.in16(outM), .clk(clk), .load(and_3_out), .out16(register16_2_out16));
  PC pc_1 (
    .in16({register16_1_out16[15], addressM}), .inc(1'b1), .load(JUMP), .reset(reset), .clk(clk),
    .out16({pc_1_out16[15], programcounter}));
  not not_7 (not_7_out, instruction[1]);
  not not_8 (not_8_out, instruction[2]);
  not not_9 (not_9_out, instruction[0]);
  not not_10 (not_10_out, instruction[2]);
  not not_11 (not_11_out, instruction[2]);
  not not_12 (not_12_out, instruction[0]);
  not not_13 (not_13_out, instruction[1]);
  not not_14 (not_14_out, instruction[1]);
  not not_15 (not_15_out, instruction[0]);
  and and_4 (JGT, instruction[0], not_7_out, not_8_out);
  and and_5 (JEQ, not_9_out, instruction[1], not_10_out);
  and and_6 (JGE, instruction[0], instruction[1], not_11_out);
  and and_7 (JLT, not_12_out, not_13_out, instruction[2]);
  and and_8 (JNE, instruction[0], not_14_out, instruction[2]);
  and and_9 (JLE, not_15_out, instruction[1], instruction[2]);
  and and_10 (JMP, instruction[0], instruction[1], instruction[2]);
  ALU alu_1 (
    .x16(register16_2_out16), .y16(multiplexer_2_out), .zx(instruction[11]), .nx(instruction[10]),
    .zy(instruction[9]), .ny(instruction[8]), .f(instruction[7]), .no(instruction[6]), .out16(outM), .zr(EQ),
    .ng(ng));
  and and_11 (and_11_out, JGT, GT);
  and and_12 (and_12_out, JEQ, EQ);
  and and_13 (and_13_out, JGE, GE);
  and and_14 (and_14_out, JLT, LT);
  and and_15 (and_15_out, JNE, NE);
  and and_16 (and_16_out, JLE, LE);
  and and_17 (writeM, instruction[15], instruction[3]);
  or or_4 (or_4_out, and_11_out, and_12_out, and_13_out, and_14_out, and_15_out, and_16_out, JMP);
  and and_18 (JUMP, or_4_out, instruction[15]);

  // Other names for the same wires on the sheet: instr[15:0] = instruction; destM = instruction[3];
  //   destD = instruction[4]; destA = instruction[5]; aBit = instruction[12]; isC = instruction[15]; zr = EQ

  // Notes on the sheet:
  //   should out be stored in A
  //   1xxaccccccdddjjj
  //   or out should be stored in A
  //   load the value only if instruction is an A instruction
  //   else, the register will hold the previous value
  //   A Register
  //   comparisons
  //   D Register
  //   jumps
endmodule

module ROM32K (
  input  [14:0] address15,
  input  [15:0] out16
);

  ROM #(.addrWidth(15), .dataWidth(16)) rom_1 (.addr(address15), .data(out16));
endmodule

module Computer (
  input  [12:0] addressScreen,
  input  [15:0] inKeyboard,
  input  loadKeyboard,
  input  reset,
  output [15:0] outScreen,
  output sysClock
);

  wire counter_1_q, cpubuiltin_1_writem, SYSCLKX2;
  wire [14:0] cpubuiltin_1_addressm, cpubuiltin_1_programcounter;
  wire [15:0] cpubuiltin_1_outm, memorywithio_1_out16, rom_1_data;

  ROM #(.addrWidth(15), .dataWidth(16)) rom_1 (.addr(cpubuiltin_1_programcounter), .data(rom_1_data));
  CPUBuiltIn cpubuiltin_1 (
    .reset(reset), .clk(sysClock), .inM(memorywithio_1_out16), .instruction(rom_1_data),
    .outM(cpubuiltin_1_outm), .writeM(cpubuiltin_1_writem), .addressM(cpubuiltin_1_addressm),
    .programcounter(cpubuiltin_1_programcounter));
  Clock clock_1 (.out(SYSCLKX2));
  MemoryWithIO memorywithio_1 (
    .load(cpubuiltin_1_writem), .address15(cpubuiltin_1_addressm), .in16(cpubuiltin_1_outm),
    .addressScreen(addressScreen), .loadKbd(loadKeyboard), .clk_2x(SYSCLKX2), .inKbd(inKeyboard),
    .clk(sysClock), .out16(memorywithio_1_out16), .outScreen(outScreen));
  not not_1 (sysClock, counter_1_q);
  Counter #(.max('h1), .width(1)) counter_1 (.Q(counter_1_q), .clk(SYSCLKX2));  // open: load, D, count, carry, up, clr

  // Other names for the same wires on the sheet: SYSCLK = sysClock

  // Notes on the sheet:
  //   contents of rom_1 (hex, n*v repeats v):
  //   0 fc10 17 e306 10 e308 4000 ec10 11 e308 11 fc20 ee88 11 fc10 20 e090 11 e308 10 fc98 a e301 17 ea87
  //   2XSYSCLK
endmodule

module ALUBuiltIn (
  input  zx,
  input  nx,
  input  zy,
  input  ny,
  input  f,
  input  no,
  input  [15:0] x16,
  input  [15:0] y16,
  output [15:0] out16,
  output zr,
  output ng
);

  wire [15:0] adder_1_out, and_1_out, multiplexer_1_out, multiplexer_2_out, multiplexer_3_out,
       multiplexer_4_out, multiplexer_5_out, not_1_out, not_2_out, not_3_out;

  Multiplexer #(.width(16)) multiplexer_1 (.in0(x16), .in1({16{1'b0}}), .out(multiplexer_1_out), .sel(zx));
  Multiplexer #(.width(16)) multiplexer_2 (.in0(y16), .in1({16{1'b0}}), .out(multiplexer_2_out), .sel(zy));
  assign not_1_out = ~multiplexer_1_out;  // NOT_Gate not_1, 16 bits wide
  assign not_2_out = ~multiplexer_2_out;  // NOT_Gate not_2, 16 bits wide
  Multiplexer #(.width(16)) multiplexer_3 (.in0(multiplexer_1_out), .in1(not_1_out), .out(multiplexer_3_out), .sel(nx));
  Multiplexer #(.width(16)) multiplexer_4 (.in0(multiplexer_2_out), .in1(not_2_out), .out(multiplexer_4_out), .sel(ny));
  assign and_1_out = multiplexer_3_out & multiplexer_4_out;  // AND_Gate and_1, 16 bits wide
  Adder #(.width(16)) adder_1 (.a(multiplexer_3_out), .b(multiplexer_4_out), .out(adder_1_out));  // open: cin, cout
  Multiplexer #(.width(16)) multiplexer_5 (.in0(and_1_out), .in1(adder_1_out), .out(multiplexer_5_out), .sel(f));
  assign not_3_out = ~multiplexer_5_out;  // NOT_Gate not_3, 16 bits wide
  Multiplexer #(.width(16)) multiplexer_6 (.in0(multiplexer_5_out), .in1(not_3_out), .out({ng, out16[14:0]}), .sel(no));
  nor nor_1 (zr, out16[0], out16[1], out16[2], out16[3], out16[4], out16[5], out16[6], out16[7], out16[8], out16[9], out16[10], out16[11], out16[12], out16[13], out16[14], ng);

  assign out16[15] = ng;
endmodule

module CPUBuiltIn (
  input  [15:0] instruction,
  input  [15:0] inM,
  input  reset,
  input  clk,
  output [15:0] outM,
  output writeM,
  output [14:0] addressM,
  output [14:0] programcounter
);

  wire and_3_out, and_11_out, and_12_out, and_13_out, and_14_out, and_15_out, and_16_out, EQ, GE, GT, isA,
       JEQ, JGE, JGT, JLE, JLT, JMP, JNE, JUMP, LE, LT, nand_1_out, NE, ng, not_2_out, not_3_out, not_4_out,
       not_5_out, not_7_out, not_8_out, not_9_out, not_10_out, not_11_out, not_12_out, not_13_out,
       not_14_out, not_15_out, or_1_out, or_4_out, or_5_out;
  wire [15:0] multiplexer_1_out, multiplexer_2_out, multiplexer_3_out, register_2_q;
  wire [15:15] counter_1_q, register_1_q;

  Multiplexer #(.width(16)) multiplexer_1 (.in0(outM), .in1(instruction), .out(multiplexer_1_out), .sel(nand_1_out));
  nand nand_1 (nand_1_out, instruction[15], instruction[5]);
  not not_1 (isA, instruction[15]);
  or or_1 (or_1_out, isA, instruction[5]);
  Register #(.width(16)) register_1 (
    .D(multiplexer_1_out), .en(or_1_out), .clk(clk), .Q({register_1_q[15], addressM}));  // open: clr
  not not_2 (not_2_out, EQ);
  not not_3 (not_3_out, ng);
  not not_4 (not_4_out, ng);
  not not_5 (not_5_out, EQ);
  Multiplexer #(.width(16)) multiplexer_2 (
    .in0({register_1_q[15], addressM}), .in1(inM), .out(multiplexer_2_out), .sel(instruction[12]));
  and and_1 (GT, not_2_out, not_3_out);
  or or_2 (GE, EQ, not_4_out);
  and and_2 (LT, not_5_out, ng);
  not not_6 (NE, EQ);
  or or_3 (LE, EQ, ng);
  and and_3 (and_3_out, instruction[15], instruction[4]);
  Register #(.width(16)) register_2 (.D(outM), .en(and_3_out), .clk(clk), .Q(register_2_q));  // open: clr
  Multiplexer #(.width(16)) multiplexer_3 (
    .in0({register_1_q[15], addressM}), .in1({16{1'b0}}), .out(multiplexer_3_out), .sel(reset));
  or or_4 (or_4_out, reset, JUMP);
  Counter #(.max('hffff), .width(16)) counter_1 (
    .load(or_4_out), .D(multiplexer_3_out), .count(1'b1), .Q({counter_1_q[15], programcounter}), .clk(clk));  // open: carry, up, clr
  not not_7 (not_7_out, instruction[1]);
  not not_8 (not_8_out, instruction[2]);
  not not_9 (not_9_out, instruction[0]);
  not not_10 (not_10_out, instruction[2]);
  not not_11 (not_11_out, instruction[2]);
  not not_12 (not_12_out, instruction[0]);
  not not_13 (not_13_out, instruction[1]);
  not not_14 (not_14_out, instruction[1]);
  not not_15 (not_15_out, instruction[0]);
  and and_4 (JGT, instruction[0], not_7_out, not_8_out);
  and and_5 (JEQ, not_9_out, instruction[1], not_10_out);
  and and_6 (JGE, instruction[0], instruction[1], not_11_out);
  and and_7 (JLT, not_12_out, not_13_out, instruction[2]);
  and and_8 (JNE, instruction[0], not_14_out, instruction[2]);
  and and_9 (JLE, not_15_out, instruction[1], instruction[2]);
  and and_10 (JMP, instruction[0], instruction[1], instruction[2]);
  ALUBuiltIn alubuiltin_1 (
    .x16(register_2_q), .y16(multiplexer_2_out), .zx(instruction[11]), .nx(instruction[10]),
    .zy(instruction[9]), .ny(instruction[8]), .f(instruction[7]), .no(instruction[6]), .out16(outM), .zr(EQ),
    .ng(ng));
  and and_11 (and_11_out, JGT, GT);
  and and_12 (and_12_out, JEQ, EQ);
  and and_13 (and_13_out, JGE, GE);
  and and_14 (and_14_out, JLT, LT);
  and and_15 (and_15_out, JNE, NE);
  and and_16 (and_16_out, JLE, LE);
  and and_17 (writeM, instruction[15], instruction[3]);
  or or_5 (or_5_out, and_11_out, and_12_out, and_13_out, and_14_out, and_15_out, and_16_out, JMP);
  and and_18 (JUMP, or_5_out, instruction[15]);

  // Other names for the same wires on the sheet: instr[15:0] = instruction; destM = instruction[3];
  //   destD = instruction[4]; destA = instruction[5]; aBit = instruction[12]; isC = instruction[15]; zr = EQ

  // Notes on the sheet:
  //   should out be stored in A
  //   1xxaccccccdddjjj
  //   or out should be stored in A
  //   load the value only if instruction is an A instruction
  //   else, the register will hold the previous value
  //   A Register
  //   comparisons
  //   D Register
  //   PC (counter)
  //   jumps
endmodule

module Computer128x128 (
  input  reset
);

  wire button_34_out, button_68_out, button_69_out, clk;
  wire [2:0] button_64_out, button_66_out, button_70_out;
  wire [2:2] rgb_video_1_p6;
  wire [6:0] rgb_video_1_p4, rgb_video_1_p5;
  wire [10:0] button_12_out, button_75_out, button_86_out;
  wire [11:0] button_9_out, button_11_out, button_79_out, button_83_out;
  wire [12:0] button_1_out, videocard128x128_1_addressm;
  wire [13:0] button_5_out;
  wire [15:0] computer_1_outscreen, kbd;

  Button button_1 (.out(button_1_out[0]));
  Button button_2 (.out(button_1_out[1]));
  Button button_3 (.out(button_1_out[2]));
  Button button_4 (.out(button_1_out[3]));
  Button button_5 (.out(button_5_out[0]));
  Button button_6 (.out(button_5_out[1]));
  Button button_7 (.out(button_5_out[2]));
  Button button_8 (.out(button_5_out[3]));
  Button button_9 (.out(button_9_out[0]));
  Button button_10 (.out(button_9_out[1]));
  Button button_11 (.out(button_11_out[0]));
  Button button_12 (.out(button_12_out[0]));
  Button button_13 (.out(button_12_out[1]));
  Button button_14 (.out(button_1_out[4]));
  Button button_15 (.out(button_1_out[5]));
  Button button_16 (.out(button_1_out[6]));
  Button button_17 (.out(button_1_out[7]));
  Button button_18 (.out(button_5_out[4]));
  Button button_19 (.out(button_5_out[5]));
  Button button_20 (.out(button_5_out[6]));
  Button button_21 (.out(button_5_out[7]));
  Button button_22 (.out(button_9_out[2]));
  Button button_23 (.out(button_9_out[3]));
  Button button_24 (.out(button_9_out[4]));
  Button button_25 (.out(button_9_out[5]));
  Button button_26 (.out(button_11_out[1]));
  Button button_27 (.out(button_11_out[2]));
  Button button_28 (.out(button_11_out[3]));
  Button button_29 (.out(button_11_out[4]));
  Button button_30 (.out(button_12_out[2]));
  Button button_31 (.out(button_12_out[3]));
  Button button_32 (.out(button_12_out[4]));
  Button button_33 (.out(button_12_out[5]));
  Button button_34 (.out(button_34_out));
  // RGB_Video #(.cursor("No Cursor")) rgb_video_1: pin names not known; wires that end beside it: reset, clk, 1'b1, rgb_video_1_p4, rgb_video_1_p5, {3{rgb_video_1_p6[2]}}
  Button button_35 (.out(button_1_out[8]));
  Button button_36 (.out(button_1_out[9]));
  Button button_37 (.out(button_1_out[10]));
  Button button_38 (.out(button_1_out[11]));
  Button button_39 (.out(button_5_out[8]));
  Button button_40 (.out(button_5_out[9]));
  Button button_41 (.out(button_5_out[10]));
  Button button_42 (.out(button_5_out[11]));
  Button button_43 (.out(button_9_out[6]));
  Button button_44 (.out(button_9_out[7]));
  Button button_45 (.out(button_9_out[8]));
  Button button_46 (.out(button_9_out[9]));
  Button button_47 (.out(button_11_out[5]));
  Button button_48 (.out(button_11_out[6]));
  Button button_49 (.out(button_11_out[7]));
  Button button_50 (.out(button_11_out[8]));
  Button button_51 (.out(button_12_out[6]));
  Button button_52 (.out(button_12_out[7]));
  Button button_53 (.out(button_12_out[8]));
  Button button_54 (.out(button_12_out[9]));
  Computer computer_1 (
    .loadKeyboard(1'b1), .addressScreen(videocard128x128_1_addressm), .inKeyboard(kbd), .reset(reset),
    .sysClock(clk), .outScreen(computer_1_outscreen));
  Button button_55 (.out(button_1_out[12]));
  Button button_56 (.out(button_5_out[12]));
  Button button_57 (.out(button_5_out[13]));
  Button button_58 (.out(button_9_out[10]));
  Button button_59 (.out(button_9_out[11]));
  Button button_60 (.out(button_11_out[9]));
  Button button_61 (.out(button_11_out[10]));
  Button button_62 (.out(button_11_out[11]));
  Button button_63 (.out(button_12_out[10]));
  KBDEncoder kbdencoder_1 (
    .qtoClosingbracket(button_9_out), .bactick2backspace(button_5_out), .esc2f12(button_1_out),
    .space(button_34_out), .enter(button_68_out), .ins2pgup(button_64_out), .del2pgdwn(button_66_out),
    .up(button_69_out), .Backslash2Slash(button_12_out), .lt2rt(button_70_out), .verbar2qstn(button_86_out),
    .A2Tilde(button_83_out), .Q2closingcurly(button_79_out), .excl2plus(button_75_out),
    .a2hashtag(button_11_out), .value(kbd));
  Button button_64 (.out(button_64_out[0]));
  Button button_65 (.out(button_64_out[1]));
  Button button_66 (.out(button_66_out[0]));
  Button button_67 (.out(button_66_out[1]));
  Button button_68 (.out(button_68_out));
  Button button_69 (.out(button_69_out));
  Button button_70 (.out(button_70_out[0]));
  Button button_71 (.out(button_70_out[1]));
  Button button_72 (.out(button_64_out[2]));
  Button button_73 (.out(button_66_out[2]));
  Button button_74 (.out(button_70_out[2]));
  Button button_75 (.out(button_75_out[0]));
  Button button_76 (.out(button_75_out[1]));
  Button button_77 (.out(button_75_out[2]));
  Button button_78 (.out(button_75_out[3]));
  Button button_79 (.out(button_79_out[0]));
  Button button_80 (.out(button_79_out[1]));
  Button button_81 (.out(button_79_out[2]));
  Button button_82 (.out(button_79_out[3]));
  Button button_83 (.out(button_83_out[0]));
  Button button_84 (.out(button_83_out[1]));
  Button button_85 (.out(button_83_out[2]));
  Button button_86 (.out(button_86_out[0]));
  Button button_87 (.out(button_86_out[1]));
  Button button_88 (.out(button_86_out[2]));
  Button button_89 (.out(button_86_out[3]));
  VideoCard128x128 videocard128x128_1 (
    .reset(reset), .clk(clk), .inM(computer_1_outscreen), .y(rgb_video_1_p5), .x(rgb_video_1_p4),
    .addressM(videocard128x128_1_addressm), .outValue(rgb_video_1_p6[2]));
  Button button_90 (.out(button_75_out[4]));
  Button button_91 (.out(button_75_out[5]));
  Button button_92 (.out(button_75_out[6]));
  Button button_93 (.out(button_75_out[7]));
  Button button_94 (.out(button_79_out[4]));
  Button button_95 (.out(button_79_out[5]));
  Button button_96 (.out(button_79_out[6]));
  Button button_97 (.out(button_79_out[7]));
  Button button_98 (.out(button_83_out[3]));
  Button button_99 (.out(button_83_out[4]));
  Button button_100 (.out(button_83_out[5]));
  Button button_101 (.out(button_83_out[6]));
  Button button_102 (.out(button_86_out[4]));
  Button button_103 (.out(button_86_out[5]));
  Button button_104 (.out(button_86_out[6]));
  Button button_105 (.out(button_86_out[7]));
  Button button_106 (.out(button_75_out[8]));
  Button button_107 (.out(button_75_out[9]));
  Button button_108 (.out(button_75_out[10]));
  Button button_109 (.out(button_79_out[8]));
  Button button_110 (.out(button_79_out[9]));
  Button button_111 (.out(button_79_out[10]));
  Button button_112 (.out(button_79_out[11]));
  Button button_113 (.out(button_83_out[7]));
  Button button_114 (.out(button_83_out[8]));
  Button button_115 (.out(button_83_out[9]));
  Button button_116 (.out(button_83_out[10]));
  Button button_117 (.out(button_86_out[8]));
  Button button_118 (.out(button_86_out[9]));
  Button button_119 (.out(button_86_out[10]));
  Button button_120 (.out(button_83_out[11]));

  // Notes on the sheet:
  //   esc
  //   f1
  //   f2
  //   f3
  //   `
  //   1
  //   2
  //   3
  //   q
  //   w
  //   a
  //   \
  //   z
  //   f4
  //   f5
  //   f6
  //   f7
  //   6
  //   4
  //   5
  //   7
  //   e
  //   r
  //   t
  //   y
  //   g
  //   s
  //   d
  //   f
  //   h
  //   x
  //   c
  //   v
  //   b
  //   sp
  //   f8
  //   f9
  //   f10
  //   f11
  //   8
  //   9
  //   0
  //   -
  //   p
  //   u
  //   i
  //   o
  //   j
  //   k
  //   l
  //   ;
  //   ,
  //   n
  //   m
  //   .
  //   f12
  //   =
  //   bsp
  //   [
  //   ]
  //   ent
  //   '
  //   #
  //   /
  //   ins
  //   hme
  //   del
  //   end
  //   pgd
  //   up
  //   lt
  //   dn
  //   rt
  //   pgu
  //   !
  //   "
  //   %
  //   ^
  //   $
  //   Q
  //   W
  //   E
  //   R
  //   A
  //   S
  //   D
  //   |
  //   Z
  //   X
  //   C
  //   &
  //   (
  //   )
  //   *
  //   T
  //   Y
  //   U
  //   I
  //   F
  //   G
  //   H
  //   J
  //   K
  //   V
  //   B
  //   N
  //   M
  //   _
  //   +
  //   O
  //   P
  //   {
  //   }
  //   L
  //   :
  //   @
  //   ~
  //   <
  //   >
  //   ?
endmodule

module Computer512x256 (
  input  reset
);

  wire button_34_out, button_68_out, button_69_out, clk, rgb_video_1_p3;
  wire [2:0] button_64_out, button_66_out, button_70_out;
  wire [2:2] rgb_video_1_p6;
  wire [7:0] rgb_video_1_p4, rgb_video_1_p5;
  wire [8:8] rgb_video_2_p3;
  wire [10:0] button_12_out, button_75_out, button_86_out;
  wire [11:0] button_9_out, button_11_out, button_79_out, button_83_out;
  wire [12:0] button_1_out, videocard512x256_1_addressm;
  wire [13:0] button_5_out;
  wire [15:0] computer_1_outscreen, kbd;

  // RGB_Video #(.cursor("No Cursor"), .height(256), .width(256)) rgb_video_1: pin names not known; wires that end beside it: reset, clk, rgb_video_1_p3, rgb_video_1_p4, rgb_video_1_p5, {3{rgb_video_1_p6[2]}}
  not not_1 (rgb_video_1_p3, rgb_video_2_p3[8]);
  Button button_1 (.out(button_1_out[0]));
  Button button_2 (.out(button_1_out[1]));
  Button button_3 (.out(button_1_out[2]));
  Button button_4 (.out(button_1_out[3]));
  Button button_5 (.out(button_5_out[0]));
  Button button_6 (.out(button_5_out[1]));
  Button button_7 (.out(button_5_out[2]));
  Button button_8 (.out(button_5_out[3]));
  Button button_9 (.out(button_9_out[0]));
  Button button_10 (.out(button_9_out[1]));
  Button button_11 (.out(button_11_out[0]));
  Button button_12 (.out(button_12_out[0]));
  Button button_13 (.out(button_12_out[1]));
  Button button_14 (.out(button_1_out[4]));
  Button button_15 (.out(button_1_out[5]));
  Button button_16 (.out(button_1_out[6]));
  Button button_17 (.out(button_1_out[7]));
  Button button_18 (.out(button_5_out[4]));
  Button button_19 (.out(button_5_out[5]));
  Button button_20 (.out(button_5_out[6]));
  Button button_21 (.out(button_5_out[7]));
  Button button_22 (.out(button_9_out[2]));
  Button button_23 (.out(button_9_out[3]));
  Button button_24 (.out(button_9_out[4]));
  Button button_25 (.out(button_9_out[5]));
  Button button_26 (.out(button_11_out[1]));
  Button button_27 (.out(button_11_out[2]));
  Button button_28 (.out(button_11_out[3]));
  Button button_29 (.out(button_11_out[4]));
  Button button_30 (.out(button_12_out[2]));
  Button button_31 (.out(button_12_out[3]));
  Button button_32 (.out(button_12_out[4]));
  Button button_33 (.out(button_12_out[5]));
  Button button_34 (.out(button_34_out));
  Button button_35 (.out(button_1_out[8]));
  Button button_36 (.out(button_1_out[9]));
  Button button_37 (.out(button_1_out[10]));
  Button button_38 (.out(button_1_out[11]));
  Button button_39 (.out(button_5_out[8]));
  Button button_40 (.out(button_5_out[9]));
  Button button_41 (.out(button_5_out[10]));
  Button button_42 (.out(button_5_out[11]));
  Button button_43 (.out(button_9_out[6]));
  Button button_44 (.out(button_9_out[7]));
  Button button_45 (.out(button_9_out[8]));
  Button button_46 (.out(button_9_out[9]));
  Button button_47 (.out(button_11_out[5]));
  Button button_48 (.out(button_11_out[6]));
  Button button_49 (.out(button_11_out[7]));
  Button button_50 (.out(button_11_out[8]));
  Button button_51 (.out(button_12_out[6]));
  Button button_52 (.out(button_12_out[7]));
  Button button_53 (.out(button_12_out[8]));
  Button button_54 (.out(button_12_out[9]));
  Computer computer_1 (
    .loadKeyboard(1'b1), .addressScreen(videocard512x256_1_addressm), .inKeyboard(kbd), .reset(reset),
    .sysClock(clk), .outScreen(computer_1_outscreen));
  Button button_55 (.out(button_1_out[12]));
  Button button_56 (.out(button_5_out[12]));
  Button button_57 (.out(button_5_out[13]));
  Button button_58 (.out(button_9_out[10]));
  Button button_59 (.out(button_9_out[11]));
  Button button_60 (.out(button_11_out[9]));
  Button button_61 (.out(button_11_out[10]));
  Button button_62 (.out(button_11_out[11]));
  Button button_63 (.out(button_12_out[10]));
  KBDEncoder kbdencoder_1 (
    .qtoClosingbracket(button_9_out), .bactick2backspace(button_5_out), .esc2f12(button_1_out),
    .space(button_34_out), .enter(button_68_out), .ins2pgup(button_64_out), .del2pgdwn(button_66_out),
    .up(button_69_out), .Backslash2Slash(button_12_out), .lt2rt(button_70_out), .verbar2qstn(button_86_out),
    .A2Tilde(button_83_out), .Q2closingcurly(button_79_out), .excl2plus(button_75_out),
    .a2hashtag(button_11_out), .value(kbd));
  Button button_64 (.out(button_64_out[0]));
  Button button_65 (.out(button_64_out[1]));
  Button button_66 (.out(button_66_out[0]));
  Button button_67 (.out(button_66_out[1]));
  Button button_68 (.out(button_68_out));
  Button button_69 (.out(button_69_out));
  Button button_70 (.out(button_70_out[0]));
  Button button_71 (.out(button_70_out[1]));
  // RGB_Video #(.cursor("No Cursor"), .height(256), .width(256)) rgb_video_2: pin names not known; wires that end beside it: reset, clk, rgb_video_2_p3[8], rgb_video_1_p4, rgb_video_1_p5, {3{rgb_video_1_p6[2]}}
  Button button_72 (.out(button_64_out[2]));
  Button button_73 (.out(button_66_out[2]));
  Button button_74 (.out(button_70_out[2]));
  Button button_75 (.out(button_75_out[0]));
  Button button_76 (.out(button_75_out[1]));
  Button button_77 (.out(button_75_out[2]));
  Button button_78 (.out(button_75_out[3]));
  Button button_79 (.out(button_79_out[0]));
  Button button_80 (.out(button_79_out[1]));
  Button button_81 (.out(button_79_out[2]));
  Button button_82 (.out(button_79_out[3]));
  Button button_83 (.out(button_83_out[0]));
  Button button_84 (.out(button_83_out[1]));
  Button button_85 (.out(button_83_out[2]));
  Button button_86 (.out(button_86_out[0]));
  Button button_87 (.out(button_86_out[1]));
  Button button_88 (.out(button_86_out[2]));
  Button button_89 (.out(button_86_out[3]));
  VideoCard512x256 videocard512x256_1 (
    .reset(reset), .clk(clk), .inM(computer_1_outscreen), .y(rgb_video_1_p5),
    .x({rgb_video_2_p3[8], rgb_video_1_p4}), .addressM(videocard512x256_1_addressm),
    .outValue(rgb_video_1_p6[2]));
  Button button_90 (.out(button_75_out[4]));
  Button button_91 (.out(button_75_out[5]));
  Button button_92 (.out(button_75_out[6]));
  Button button_93 (.out(button_75_out[7]));
  Button button_94 (.out(button_79_out[4]));
  Button button_95 (.out(button_79_out[5]));
  Button button_96 (.out(button_79_out[6]));
  Button button_97 (.out(button_79_out[7]));
  Button button_98 (.out(button_83_out[3]));
  Button button_99 (.out(button_83_out[4]));
  Button button_100 (.out(button_83_out[5]));
  Button button_101 (.out(button_83_out[6]));
  Button button_102 (.out(button_86_out[4]));
  Button button_103 (.out(button_86_out[5]));
  Button button_104 (.out(button_86_out[6]));
  Button button_105 (.out(button_86_out[7]));
  Button button_106 (.out(button_75_out[8]));
  Button button_107 (.out(button_75_out[9]));
  Button button_108 (.out(button_75_out[10]));
  Button button_109 (.out(button_79_out[8]));
  Button button_110 (.out(button_79_out[9]));
  Button button_111 (.out(button_79_out[10]));
  Button button_112 (.out(button_79_out[11]));
  Button button_113 (.out(button_83_out[7]));
  Button button_114 (.out(button_83_out[8]));
  Button button_115 (.out(button_83_out[9]));
  Button button_116 (.out(button_83_out[10]));
  Button button_117 (.out(button_86_out[8]));
  Button button_118 (.out(button_86_out[9]));
  Button button_119 (.out(button_86_out[10]));
  Button button_120 (.out(button_83_out[11]));

  // Notes on the sheet:
  //   esc
  //   f1
  //   f2
  //   f3
  //   `
  //   1
  //   2
  //   3
  //   q
  //   w
  //   a
  //   \
  //   z
  //   f4
  //   f5
  //   f6
  //   f7
  //   6
  //   4
  //   5
  //   7
  //   e
  //   r
  //   t
  //   y
  //   g
  //   s
  //   d
  //   f
  //   h
  //   x
  //   c
  //   v
  //   b
  //   sp
  //   f8
  //   f9
  //   f10
  //   f11
  //   8
  //   9
  //   0
  //   -
  //   p
  //   u
  //   i
  //   o
  //   j
  //   k
  //   l
  //   ;
  //   ,
  //   n
  //   m
  //   .
  //   f12
  //   =
  //   bsp
  //   [
  //   ]
  //   ent
  //   '
  //   #
  //   /
  //   ins
  //   hme
  //   del
  //   end
  //   pgd
  //   up
  //   lt
  //   dn
  //   rt
  //   pgu
  //   !
  //   "
  //   %
  //   ^
  //   $
  //   Q
  //   W
  //   E
  //   R
  //   A
  //   S
  //   D
  //   |
  //   Z
  //   X
  //   C
  //   &
  //   (
  //   )
  //   *
  //   T
  //   Y
  //   U
  //   I
  //   F
  //   G
  //   H
  //   J
  //   K
  //   V
  //   B
  //   N
  //   M
  //   _
  //   +
  //   O
  //   P
  //   {
  //   }
  //   L
  //   :
  //   @
  //   ~
  //   <
  //   >
  //   ?
endmodule
